// Digital circuit address_decoder.dig as structural Verilog
module address_decoder (
  input  [15:0] ADDR_BUS,
  input  RAM_IN,
  input  VCC,
  input  GND,
  output nRAM_CS,
  output nROM_CS,
  output nCF_CS,
  output LCD_RS,
  output LCD_E
);

  wire _74138_1_pin10, nand_1_out;

  PowerSupply powersupply_1 (.VDD(VCC), .GND(GND));
  _74138 _74138_1 (
    .pin1(ADDR_BUS[13]), .pin2(ADDR_BUS[14]), .pin3(ADDR_BUS[15]), .pin4(GND), .pin5(GND), .pin6(VCC),
    .pin8(GND), .pin10(_74138_1_pin10), .pin11(nCF_CS), .pin16(VCC));  // open: pin7, pin9, pin12, pin13, pin14, pin15
  nand nand_1 (nand_1_out, _74138_1_pin10, RAM_IN);
  nand nand_2 (nROM_CS, ADDR_BUS[12], ADDR_BUS[13], ADDR_BUS[14], ADDR_BUS[15]);
  nand nand_3 (LCD_E, nand_1_out, nand_1_out);

  assign LCD_RS = ADDR_BUS[0];
  assign nRAM_CS = ADDR_BUS[15];

  // Notes on the sheet:
  //   VCC: default 1
endmodule
