// Digital circuit alu.dig as structural Verilog
module alu (
  input  [7:0] BUS,
  input  [7:0] REG_AINT,
  input  ALU_S3,
  input  ALU_S2,
  input  ALU_S1,
  input  ALU_S0,
  input  ALU_M,
  input  nALU_OUT,
  input  VCC,
  input  GND,
  input  CLK,
  input  ALU_BIN,
  input  FR_IN,
  input  nRRC_OUT,
  input  ALU_CARRY,
  input  nRAR_OUT,
  output ZF,
  output CF,
  output NF,
  output VF,
  output [7:0] ALU_BUFINT,
  output [7:0] ALU_OUTINT,
  output [3:0] FLAGS_INT
);

  wire _74157_1_pin10, _74157_1_pin11, _74157_1_pin13, _74157_1_pin14, _74181_2_pin7, _74245_1_pin19,
       _74573_1_pin11, _74573_2_pin11, and_4_out, and_5_out, bussplitter_1_d0, bussplitter_1_d1,
       bussplitter_1_d2, bussplitter_1_d3, bussplitter_1_d4, bussplitter_1_d5, bussplitter_1_d6,
       bussplitter_1_d7, bussplitter_2_d0, bussplitter_2_d1, bussplitter_2_d2, bussplitter_2_d3,
       bussplitter_2_d4, bussplitter_2_d5, bussplitter_2_d6, bussplitter_2_d7, D8, nor_1_out, nor_2_out,
       nor_3_out, nor_4_out, not_1_out, not_2_out, not_3_out, undriven, xor_1_out, xor_2_out;

  BusSplitter #(.Bits(8)) bussplitter_1 (
    .D(BUS), .OE(nALU_OUT), .D0(bussplitter_1_d0), .D1(bussplitter_1_d1), .D2(bussplitter_1_d2),
    .D3(bussplitter_1_d3), .D4(bussplitter_1_d4), .D5(bussplitter_1_d5), .D6(bussplitter_1_d6),
    .D7(bussplitter_1_d7));
  _74573 _74573_1 (
    .pin1(GND), .pin2(bussplitter_1_d0), .pin3(bussplitter_1_d1), .pin4(bussplitter_1_d2),
    .pin5(bussplitter_1_d3), .pin6(bussplitter_1_d4), .pin7(bussplitter_1_d5), .pin8(bussplitter_1_d6),
    .pin9(bussplitter_1_d7), .pin10(GND), .pin11(_74573_1_pin11), .pin12(ALU_BUFINT[7]),
    .pin13(ALU_BUFINT[6]), .pin14(ALU_BUFINT[5]), .pin15(ALU_BUFINT[4]), .pin16(ALU_BUFINT[3]),
    .pin17(ALU_BUFINT[2]), .pin18(ALU_BUFINT[1]), .pin19(ALU_BUFINT[0]), .pin20(VCC));
  and and_1 (_74573_1_pin11, ALU_BIN, CLK);
  _74245 _74245_1 (
    .pin1(VCC), .pin2(REG_AINT[1]), .pin3(REG_AINT[2]), .pin4(REG_AINT[3]), .pin5(REG_AINT[4]),
    .pin6(REG_AINT[5]), .pin7(REG_AINT[6]), .pin8(REG_AINT[7]), .pin9(D8), .pin10(GND),
    .pin11(bussplitter_1_d7), .pin12(bussplitter_1_d6), .pin13(bussplitter_1_d5), .pin14(bussplitter_1_d4),
    .pin15(bussplitter_1_d3), .pin16(bussplitter_1_d2), .pin17(bussplitter_1_d1), .pin18(bussplitter_1_d0),
    .pin19(_74245_1_pin19), .pin20(VCC));
  BusSplitter #(.Bits(8)) bussplitter_2 (
    .D(REG_AINT), .OE(VCC), .D0(bussplitter_2_d0), .D1(bussplitter_2_d1), .D2(bussplitter_2_d2),
    .D3(bussplitter_2_d3), .D4(bussplitter_2_d4), .D5(bussplitter_2_d5), .D6(bussplitter_2_d6),
    .D7(bussplitter_2_d7));
  and and_2 (_74245_1_pin19, nRAR_OUT, nRRC_OUT);
  LED led_1 (.in(ALU_BUFINT[0]));
  LED led_2 (.in(ALU_BUFINT[1]));
  LED led_3 (.in(ALU_BUFINT[2]));
  LED led_4 (.in(ALU_BUFINT[3]));
  LED led_5 (.in(ALU_BUFINT[4]));
  LED led_6 (.in(ALU_BUFINT[5]));
  LED led_7 (.in(ALU_BUFINT[6]));
  LED led_8 (.in(ALU_BUFINT[7]));
  PowerSupply powersupply_1 (.VDD(VCC), .GND(GND));
  not not_1 (not_1_out, ALU_CARRY);
  _74181 _74181_1 (
    .pin1(ALU_BUFINT[0]), .pin2(bussplitter_2_d0), .pin3(ALU_S3), .pin4(ALU_S2), .pin5(ALU_S1),
    .pin6(ALU_S0), .pin7(not_1_out), .pin8(ALU_M), .pin9(ALU_OUTINT[0]), .pin10(ALU_OUTINT[1]),
    .pin11(ALU_OUTINT[2]), .pin12(GND));  // open: pin13, pin14, pin15, pin16, pin17, pin18, pin19, pin20, pin21, pin22, pin23, pin24
  _74181 _74181_2 (
    .pin1(ALU_BUFINT[4]), .pin2(bussplitter_2_d4), .pin3(ALU_S3), .pin4(ALU_S2), .pin5(ALU_S1),
    .pin6(ALU_S0), .pin7(_74181_2_pin7), .pin8(ALU_M), .pin9(ALU_OUTINT[4]), .pin10(ALU_OUTINT[5]),
    .pin11(ALU_OUTINT[6]), .pin12(GND));  // open: pin13, pin14, pin15, pin16, pin17, pin18, pin19, pin20, pin21, pin22, pin23, pin24
  xor xor_1 (xor_1_out, ALU_OUTINT[7], bussplitter_2_d7);
  xor xor_2 (xor_2_out, ALU_BUFINT[7], bussplitter_2_d7);
  and and_3 (FLAGS_INT[0], xor_1_out, not_2_out);
  not not_2 (not_2_out, xor_2_out);
  LED led_9 (.in(ALU_OUTINT[7]));
  LED led_10 (.in(ALU_OUTINT[6]));
  LED led_11 (.in(ALU_OUTINT[5]));
  LED led_12 (.in(ALU_OUTINT[4]));
  LED led_13 (.in(ALU_OUTINT[3]));
  LED led_14 (.in(ALU_OUTINT[2]));
  LED led_15 (.in(ALU_OUTINT[1]));
  LED led_16 (.in(ALU_OUTINT[0]));
  nor nor_1 (nor_1_out, ALU_OUTINT[0], ALU_OUTINT[1]);
  nor nor_2 (nor_2_out, ALU_OUTINT[2], ALU_OUTINT[3]);
  nor nor_3 (nor_3_out, ALU_OUTINT[4], ALU_OUTINT[5]);
  nor nor_4 (nor_4_out, ALU_OUTINT[6], ALU_OUTINT[7]);
  not not_3 (not_3_out, undriven);
  _74245 _74245_2 (
    .pin1(VCC), .pin2(ALU_OUTINT[0]), .pin3(ALU_OUTINT[1]), .pin4(ALU_OUTINT[2]), .pin5(ALU_OUTINT[3]),
    .pin6(ALU_OUTINT[4]), .pin7(ALU_OUTINT[5]), .pin8(ALU_OUTINT[6]), .pin9(ALU_OUTINT[7]), .pin10(GND),
    .pin11(bussplitter_1_d7), .pin12(bussplitter_1_d6), .pin13(bussplitter_1_d5), .pin14(bussplitter_1_d4),
    .pin15(bussplitter_1_d3), .pin16(bussplitter_1_d2), .pin17(bussplitter_1_d1), .pin18(bussplitter_1_d0),
    .pin19(nALU_OUT), .pin20(VCC));
  and and_4 (and_4_out, nor_1_out, nor_2_out);
  and and_5 (and_5_out, nor_3_out, nor_4_out);
  _74157 _74157_1 (
    .pin1(nRAR_OUT), .pin2(REG_AINT[0]), .pin3(not_3_out), .pin4(FLAGS_INT[2]), .pin5(ALU_CARRY),
    .pin6(REG_AINT[0]), .pin7(D8), .pin8(GND), .pin10(_74157_1_pin10), .pin11(_74157_1_pin11),
    .pin13(_74157_1_pin13), .pin14(_74157_1_pin14), .pin15(GND), .pin16(VCC));  // open: pin9, pin12
  and and_6 (FLAGS_INT[3], and_4_out, and_5_out);
  LED led_17 (.in(FLAGS_INT[0]));
  // NotConnected on _74157_1_pin14
  // NotConnected on _74157_1_pin13
  // NotConnected on _74157_1_pin11
  // NotConnected on _74157_1_pin10
  LED led_18 (.in(FLAGS_INT[2]));
  LED led_19 (.in(ALU_OUTINT[7]));
  _74573 _74573_2 (
    .pin1(GND), .pin2(FLAGS_INT[3]), .pin3(FLAGS_INT[2]), .pin4(ALU_OUTINT[7]), .pin5(FLAGS_INT[0]),
    .pin6(GND), .pin7(GND), .pin8(GND), .pin9(GND), .pin10(GND), .pin11(_74573_2_pin11), .pin16(VF),
    .pin17(NF), .pin18(CF), .pin19(ZF), .pin20(VCC));  // open: pin12, pin13, pin14, pin15
  LED led_20 (.in(FLAGS_INT[3]));
  and and_7 (_74573_2_pin11, FR_IN, CLK);

  assign FLAGS_INT[1] = ALU_OUTINT[7];

  // Other names for the same wires on the sheet: CARRY = ALU_CARRY; D0 = REG_AINT[0]

  // Notes on the sheet:
  //   nALU_OUT: default 1
  //   VCC: default 1
  //   nRRC_OUT: default 1
  //   nRAR_OUT: default 1
  //   V
  //   N
  //   C
  //   Z
endmodule
