// Digital circuit instruction_decoder.dig as structural Verilog
module instruction_decoder (
  input  VCC,
  input  GND,
  input  [7:0] IR_BUS,
  input  STEP_0_T,
  input  STEP_1_T,
  input  STEP_2_T,
  input  STEP_3_T,
  input  VF,
  input  NF,
  input  CF,
  input  ZF,
  output nREG_AOUT,
  output nREG_BOUT,
  output nREG_COUT,
  output nREG_DOUT,
  output nREG_EOUT,
  output nREG_LOUT,
  output nREG_HOUT,
  output RAM_OUT,
  output nALU_OUT,
  output nPAIR_BCOUT,
  output nPAIR_DEOUT,
  output nPAIR_HLOUT,
  output nSP_OUT,
  output nPC_HLOUT,
  output nMAR_OUT,
  output HLT,
  output nINC_H,
  output nDEC_H,
  output nINC_SP,
  output nDEC_SP,
  output ALU_S0,
  output ALU_S1,
  output ALU_S2,
  output ALU_S3,
  output ALU_M,
  output FR_IN,
  output nJMP_L,
  output nJMP_H,
  output PC_E,
  output REG_AIN,
  output REG_BIN,
  output REG_CIN,
  output REG_DIN,
  output REG_EIN,
  output REG_LIN,
  output REG_HIN,
  output MAR_LIN,
  output MAR_HIN,
  output SP_LIN,
  output SP_HIN,
  output IR_IN,
  output REG_OUTIN,
  output ALU_BIN,
  output nREG_TMPOUT,
  output REG_TMPIN,
  output RAM_IN,
  output nRAR_OUT,
  output nRRC_OUT,
  output ALC,
  output INC_MAR,
  output SC_RST,
  output nPC_HOUT,
  output nPC_LOUT
);

  wire _74154_1_pin9, _74154_2_pin2, _74154_2_pin3, _74154_2_pin4, _74154_2_pin5, _74154_2_pin6,
       _74154_2_pin7, _74154_2_pin8, _74154_2_pin9, _74154_2_pin10, _74154_2_pin11, _74154_2_pin13,
       _74154_2_pin14, _74154_2_pin15, _74154_2_pin16, _74154_2_pin17, ADDR_MUX1, ADDR_MUX2, ADDR_MUX3,
       IN_MUX1, IN_MUX2, IN_MUX3, IN_MUX4, OUT_MUX1, OUT_MUX2, OUT_MUX3, OUT_MUX4;
  wire [7:1] eeprom_4_d;
  wire [7:4] eeprom_2_d;
  wire [7:6] eeprom_3_d;

  EEPROM #(.AddrBits(16), .Bits(8)) eeprom (
    .A({ZF, CF, NF, VF, STEP_3_T, STEP_2_T, STEP_1_T, STEP_0_T, IR_BUS}), .CS(~GND), .WE(~VCC), .OE(~GND),
    .D({ADDR_MUX3, ADDR_MUX2, ADDR_MUX1, OUT_MUX4, OUT_MUX3, OUT_MUX2, OUT_MUX1, HLT}));
  not not_1 (RAM_OUT, _74154_1_pin9);
  _74154 _74154_1 (
    .pin2(nREG_AOUT), .pin3(nREG_BOUT), .pin4(nREG_COUT), .pin5(nREG_DOUT), .pin6(nREG_EOUT),
    .pin7(nREG_LOUT), .pin8(nREG_HOUT), .pin9(_74154_1_pin9), .pin10(nALU_OUT), .pin11(nREG_TMPOUT),
    .pin12(GND), .pin13(nRRC_OUT), .pin14(nRAR_OUT), .pin15(nPC_LOUT), .pin16(nPC_HOUT), .pin18(GND),
    .pin19(GND), .pin20(OUT_MUX4), .pin21(OUT_MUX3), .pin22(OUT_MUX2), .pin23(OUT_MUX1), .pin24(VCC));  // open: pin1, pin17
  EEPROM #(.AddrBits(16), .Bits(8)) eeprom_2 (
    .A({ZF, CF, NF, VF, STEP_3_T, STEP_2_T, STEP_1_T, STEP_0_T, IR_BUS}), .CS(~GND), .WE(~VCC), .OE(~GND),
    .D({eeprom_2_d, IN_MUX4, IN_MUX3, IN_MUX2, IN_MUX1}));
  PowerSupply powersupply_1 (.VDD(VCC), .GND(GND));
  not not_2 (nINC_H, eeprom_2_d[4]);
  not not_3 (nDEC_H, eeprom_2_d[5]);
  not not_4 (nINC_SP, eeprom_2_d[6]);
  not not_5 (nDEC_SP, eeprom_2_d[7]);
  _74154 _74154_2 (
    .pin2(_74154_2_pin2), .pin3(_74154_2_pin3), .pin4(_74154_2_pin4), .pin5(_74154_2_pin5),
    .pin6(_74154_2_pin6), .pin7(_74154_2_pin7), .pin8(_74154_2_pin8), .pin9(_74154_2_pin9),
    .pin10(_74154_2_pin10), .pin11(_74154_2_pin11), .pin12(GND), .pin13(_74154_2_pin13),
    .pin14(_74154_2_pin14), .pin15(_74154_2_pin15), .pin16(_74154_2_pin16), .pin17(_74154_2_pin17),
    .pin18(GND), .pin19(GND), .pin20(IN_MUX4), .pin21(IN_MUX3), .pin22(IN_MUX2), .pin23(IN_MUX1), .pin24(VCC));  // open: pin1
  not not_6 (REG_AIN, _74154_2_pin2);
  not not_7 (REG_BIN, _74154_2_pin3);
  not not_8 (REG_CIN, _74154_2_pin4);
  not not_9 (REG_DIN, _74154_2_pin5);
  not not_10 (REG_EIN, _74154_2_pin6);
  not not_11 (REG_LIN, _74154_2_pin7);
  not not_12 (REG_HIN, _74154_2_pin8);
  not not_13 (MAR_LIN, _74154_2_pin9);
  not not_14 (MAR_HIN, _74154_2_pin10);
  not not_15 (SP_LIN, _74154_2_pin11);
  not not_16 (ALU_BIN, _74154_2_pin17);
  not not_17 (REG_OUTIN, _74154_2_pin16);
  not not_18 (REG_TMPIN, _74154_2_pin15);
  not not_19 (IR_IN, _74154_2_pin14);
  not not_20 (SP_HIN, _74154_2_pin13);
  _74154 _74154_3 (
    .pin2(nPAIR_BCOUT), .pin3(nPAIR_DEOUT), .pin4(nPAIR_HLOUT), .pin5(nSP_OUT), .pin6(nPC_HLOUT),
    .pin7(nMAR_OUT), .pin12(GND), .pin18(GND), .pin19(GND), .pin20(GND), .pin21(ADDR_MUX3),
    .pin22(ADDR_MUX2), .pin23(ADDR_MUX1), .pin24(VCC));  // open: pin1, pin8, pin9, pin10, pin11, pin13, pin14, pin15, pin16, pin17
  EEPROM #(.AddrBits(16), .Bits(8)) eeprom_3 (
    .A({ZF, CF, NF, VF, STEP_3_T, STEP_2_T, STEP_1_T, STEP_0_T, IR_BUS}), .CS(~GND), .WE(~VCC), .OE(~GND),
    .D({eeprom_3_d, FR_IN, ALU_M, ALU_S3, ALU_S2, ALU_S1, ALU_S0}));
  not not_21 (nJMP_L, eeprom_3_d[6]);
  not not_22 (nJMP_H, eeprom_3_d[7]);
  EEPROM #(.AddrBits(16), .Bits(8)) eeprom_4 (
    .A({ZF, CF, NF, VF, STEP_3_T, STEP_2_T, STEP_1_T, STEP_0_T, IR_BUS}), .CS(~GND), .WE(~VCC), .OE(~GND),
    .D({eeprom_4_d[7:5], INC_MAR, ALC, RAM_IN, eeprom_4_d[1], PC_E}));
  assign SC_RST = VCC ? eeprom_4_d[1] : 1'bz;  // Driver driver_1

  // Other names for the same wires on the sheet: IR[7:0] = IR_BUS

  // Notes on the sheet:
  //   VCC: pin 28, default 1
  //   GND: pin 14
  //   contents of eeprom (hex, n*v repeats v):
  //   b0,b0,b0,0,0,0,b0,b0,0,b0,b0,0,0,0,b0,b0,0,b0,b0,0,0,0,b0,b0,0
  //   ,b0,b0,0,0,0,b0,b0,0,b0,b0,0,0,0,b0,0,0,b0,b0,0,0,0,b0,b0,0,b0,b0
  //   ,0,0,0,b0,0,0,0,b0,0,0,0,b0,0,0,8*b0,0,8*b0,0,8*b0,0,8*b0,0,26*b0
  //   ,0,71*b0,0,b0,b0,b0,0,b0,b0,b0,0,b0,b0,b0,0,b0,b0,b0,0,b0,0,b0
  //   ,0,b0,0,b0,0,b0,b0,b0,0,b0,b0,b0,0,b0,0,b0,0,b0,0,b0,0,b0,0,b0
  //   ,0,b0,0,b0,0,b0,0,b0,0,b0,0,b0,0,0,0,22,6*0,6,30,4*0,16,0,0,42
  //   ,6*0,a,50,4*0,18,9*0,c,5*0,12,17*0,6,8,a,c,e,70,2,4,0,8,a,c,e
  //   ,70,2,4,6,0,a,c,e,70,2,4,6,8,0,c,e,70,2,4,6,8,a,0,e,70,2,4,6,8
  //   ,a,c,2,70,2,64,66,68,6a,6c,6e,1,62,4,6,8,a,c,e,70,0,4,6,8,a,c
  //   ,e,70,2,4,6,8,a,c,e,70,2,4,6,8,a,c,e,70,2,4,6,8,a,c,e,70,2,4,6
  //   ,8,a,c,e,70,2,4,6,8,a,c,e,70,2,4,6,8,a,c,e,70,2,4,6,8,a,c,e,70
  //   ,2,90,90,7*0,90,6*0,90,90,14*0,90,90,14*0,90,16*0,b0,4*0,b0,12
  //   ,0,c,4*0,b0,0,0,b0,4*0,b0,12,0,c,4*0,b0,0,0,b0,b0,0,0,0,b0,0,0
  //   ,c,b0,0,0,0,b0,0,0,b0,b0,0,0,0,b0,0,0,0,b0,0,0,0,b0,65*0,56*12
  //   ,10*0,b0,b0,b0,84,b0,6*0,b0,b0,0,0,0,b0,0,b0,88,b0,7*0,b0,0,0,0
  //   ,b0,0,b0,8e,b0,7*0,b0,0,0,0,b0,0,b0,0,b0,7*0,b0,10*0,12,15*0,12
  //   ,15*0,12,150*0,90,90,7*0,90,6*0,90,90,14*0,90,90,14*0,90,16*0
  //   ,b0,7*0,4,7*0,b0,7*0,8,7*0,b0,b0,6*0,e,b0,6*0,b0,b0,0,0,0,74,0,0,0
  //   ,b0,135*0,b0,b0,b0,86,12,6*0,b0,12,0,0,0,b0,0,b0,8a,12,7*0,12
  //   ,0,0,0,b0,0,b0,8c,12,7*0,12,0,0,0,b0,0,b0,0,12,18*0,e,15*0,e,15*0
  //   ,e,152*0,14,14,14*0,14,15*0,14,15*0,14,22*0,12,15*0,12,8*0,cc
  //   ,6*0,12,d0,7*0,c2,7*0,d0,393*0,9c,8*0,9c,6*0,9c,15*0,9c,15*0,9c
  //   ,45*0,ce,7*0,d0,409*0,9a,8*0,9a,6*0,9a,15*0,9a,15*0,9a,207*0,12
  //   ,8*0,12,6*0,12,15*0,12,15*0,12,207*0,14,8*0,14,6*0,14,15*0,14
  //   ,15*0,14,1035*0,b0,b0,b0,0,0,0,b0,b0,0,b0,b0,0,0,0,b0,b0,0,b0,b0
  //   ,0,0,0,b0,b0,0,b0,b0,0,0,0,b0,b0,0,b0,b0,0,0,0,b0,0,0,b0,b0,0,0,0
  //   ,b0,b0,0,b0,b0,0,0,0,b0,0,0,0,b0,0,0,0,b0,0,0,8*b0,0,8*b0,0,8*b0
  //   ,0,8*b0,0,26*b0,0,71*b0,0,b0,b0,b0,0,b0,b0,b0,0,b0,b0,b0,0,b0,b0,b0
  //   ,0,b0,0,b0,0,b0,0,b0,0,b0,b0,b0,0,b0,b0,b0,0,b0,0,b0,0,b0,0,b0
  //   ,0,b0,0,b0,0,b0,0,b0,0,b0,0,b0,0,b0,0,b0,0,0,0,22,6*0,6,30,4*0
  //   ,16,0,0,42,6*0,a,50,4*0,18,9*0,c,5*0,12,17*0,6,8,a,c,e,70,2,4
  //   ,0,8,a,c,e,70,2,4,6,0,a,c,e,70,2,4,6,8,0,c,e,70,2,4,6,8,a,0,e
  //   ,70,2,4,6,8,a,c,2,70,2,64,66,68,6a,6c,6e,1,62,4,6,8,a,c,e,70,0
  //   ,4,6,8,a,c,e,70,2,4,6,8,a,c,e,70,2,4,6,8,a,c,e,70,2,4,6,8,a,c
  //   ,e,70,2,4,6,8,a,c,e,70,2,4,6,8,a,c,e,70,2,4,6,8,a,c,e,70,2,4,6
  //   ,8,a,c,e,70,2,90,90,7*0,90,6*0,90,90,15*0,90,6*0,90,7*0,90,16*0
  //   ,b0,4*0,b0,12,0,c,4*0,b0,0,0,b0,4*0,b0,12,0,c,4*0,b0,0,0,b0,b0
  //   ,0,0,0,b0,0,0,c,b0,0,0,0,b0,0,0,b0,b0,0,0,0,b0,0,0,0,b0,0,0,0
  //   ,b0,65*0,56*12,10*0,b0,b0,b0,84,b0,6*0,b0,b0,0,0,0,b0,0,b0,88
  //   ,b0,7*0,b0,6*0,8e,b0,0,0,0,b0,0,b0,0,b0,0,0,0,b0,0,b0,0,b0,7*0
  //   ,b0,10*0,12,15*0,12,15*0,12,150*0,90,90,7*0,90,6*0,90,90,15*0
  //   ,90,6*0,90,7*0,90,16*0,b0,7*0,4,7*0,b0,7*0,8,7*0,b0,b0,6*0,e,b0
  //   ,6*0,b0,b0,0,0,0,74,0,0,0,b0,135*0,b0,b0,b0,86,12,6*0,b0,12,0,0,0
  //   ,b0,0,b0,8a,12,7*0,12,6*0,8c,12,0,0,0,b0,0,b0,0,12,0,0,0,b0,0
  //   ,b0,0,12,18*0,e,15*0,e,15*0,e,152*0,14,14,14*0,14,23*0,14,7*0
  //   ,14,22*0,12,15*0,12,8*0,cc,6*0,12,d0,7*0,c2,7*0,d0,393*0,9c,8*0
  //   ,9c,6*0,9c,23*0,9c,7*0,9c,45*0,ce,7*0,d0,409*0,9a,8*0,9a,6*0,9a
  //   ,23*0,9a,7*0,9a,207*0,12,8*0,12,6*0,12,23*0,12,7*0,12,207*0,14
  //   ,8*0,14,6*0,14,23*0,14,7*0,14,1035*0,b0,b0,b0,0,0,0,b0,b0,0,b0,b0
  //   ,0,0,0,b0,b0,0,b0,b0,0,0,0,b0,b0,0,b0,b0,0,0,0,b0,b0,0,b0,b0,0,0,0
  //   ,b0,0,0,b0,b0,0,0,0,b0,b0,0,b0,b0,0,0,0,b0,0,0,0,b0,0,0,0,b0,0,0
  //   ,8*b0,0,8*b0,0,8*b0,0,8*b0,0,26*b0,0,71*b0,0,b0,b0,b0,0,b0,b0,b0
  //   ,0,b0,b0,b0,0,b0,b0,b0,0,b0,0,b0,0,b0,0,b0,0,b0,b0,b0,0,b0,b0,b0
  //   ,0,b0,0,b0,0,b0,0,b0,0,b0,0,b0,0,b0,0,b0,0,b0,0,b0,0,b0,0,b0,0,0,0
  //   ,22,6*0,6,30,4*0,16,0,0,42,6*0,a,50,4*0,18,9*0,c,5*0,12,17*0,6
  //   ,8,a,c,e,70,2,4,0,8,a,c,e,70,2,4,6,0,a,c,e,70,2,4,6,8,0,c,e,70
  //   ,2,4,6,8,a,0,e,70,2,4,6,8,a,c,2,70,2,64,66,68,6a,6c,6e,1,62,4
  //   ,6,8,a,c,e,70,0,4,6,8,a,c,e,70,2,4,6,8,a,c,e,70,2,4,6,8,a,c,e
  //   ,70,2,4,6,8,a,c,e,70,2,4,6,8,a,c,e,70,2,4,6,8,a,c,e,70,2,4,6,8
  //   ,a,c,e,70,2,4,6,8,a,c,e,70,2,90,90,7*0,90,6*0,90,90,14*0,90,90
  //   ,22*0,90,8*0,b0,4*0,b0,12,0,c,4*0,b0,0,0,b0,4*0,b0,12,0,c,4*0
  //   ,b0,0,0,b0,b0,0,0,0,b0,0,0,c,b0,0,0,0,b0,0,0,b0,b0,0,0,0,b0,0,0,0
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  //   contents of eeprom_2 (hex, n*v repeats v):
  //   c,c,c,0,0,0,c,c,0,c,c,0,0,0,c,c,0,c,c,0,0,0,c,c,0,c,c,0,0,0,c,c
  //   ,0,c,c,0,0,0,c,0,0,c,c,0,0,0,c,c,0,c,c,0,0,0,c,0,0,0,c,0,0,0,c
  //   ,0,0,8*c,0,8*c,0,8*c,0,8*c,0,26*c,0,71*c,0,c,c,c,0,c,c,c,0,c,c,c
  //   ,0,c,c,c,0,c,0,c,0,c,0,c,0,c,c,c,0,c,c,c,0,c,0,c,0,c,0,c,0,c,0
  //   ,c,0,c,0,c,0,c,0,c,0,c,0,c,10*0,1,1,4*0,1,9*0,1,1,4*0,1,9*0,1
  //   ,5*0,1,17*0,7*2,3,0,6*3,4,4,0,5*4,5,5,5,0,4*5,4*6,0,6,6,6,5*7
  //   ,e,7,7,8*0,7*1,0,64*f,0,3,0,0,0,80,11*0,5,0,0,0,80,11*0,6,0,0,0
  //   ,80,27*0,3,4*0,2,1,0,f,4*0,3,0,0,5,4*0,4,1,0,f,4*0,5,0,0,6,8,0,0,0
  //   ,6,0,0,f,8,0,0,0,7,0,0,a,8,0,0,0,d,0,0,0,8,0,0,0,1,65*0,56*1,8*0
  //   ,40,40,d,d,d,0,f,0,0,40,0,0,0,d,f,0,40,40,d,0,d,0,f,7*0,f,0,40,40
  //   ,d,0,d,0,f,7*0,f,0,40,0,d,0,d,0,f,7*0,f,10*0,6,15*0,6,15*0,6,151*0
  //   ,2,0,0,0,80,11*0,4,0,0,0,80,11*0,7,0,0,0,80,27*0,2,7*0,1,7*0,4
  //   ,7*0,1,7*0,7,9,6*0,1,9,6*0,b,9,7*0,9,133*0,40,40,0,0,f,0,1,0,0
  //   ,40,0,0,0,f,1,0,40,40,0,0,f,0,1,7*0,1,0,40,40,0,0,f,0,1,7*0,1
  //   ,0,40,0,0,0,f,0,1,18*0,f,15*0,f,15*0,f,223*0,7,15*0,7,15*0,7,6
  //   ,15*0,1,137*0,80,8*0,80,6*0,80,15*0,80,15*0,80,309*0,7,153*0,80
  //   ,8*0,80,6*0,80,15*0,80,15*0,80,1803*0,c,c,c,0,0,0,c,c,0,c,c,0,0,0
  //   ,c,c,0,c,c,0,0,0,c,c,0,c,c,0,0,0,c,c,0,c,c,0,0,0,c,0,0,c,c,0,0,0
  //   ,c,c,0,c,c,0,0,0,c,0,0,0,c,0,0,0,c,0,0,8*c,0,8*c,0,8*c,0,8*c,0
  //   ,26*c,0,71*c,0,c,c,c,0,c,c,c,0,c,c,c,0,c,c,c,0,c,0,c,0,c,0,c,0
  //   ,c,c,c,0,c,c,c,0,c,0,c,0,c,0,c,0,c,0,c,0,c,0,c,0,c,0,c,0,c,0,c
  //   ,10*0,1,1,4*0,1,9*0,1,1,4*0,1,9*0,1,5*0,1,17*0,7*2,3,0,6*3,4,4
  //   ,0,5*4,5,5,5,0,4*5,4*6,0,6,6,6,5*7,e,7,7,8*0,7*1,0,64*f,0,3,0,0,0
  //   ,80,11*0,5,0,0,0,80,11*0,6,0,0,0,80,27*0,3,4*0,2,1,0,f,4*0,3,0,0
  //   ,5,4*0,4,1,0,f,4*0,5,0,0,6,8,0,0,0,6,0,0,f,8,0,0,0,7,0,0,a,8,0,0,0
  //   ,d,0,0,0,8,0,0,0,1,65*0,56*1,8*0,40,40,d,d,d,0,f,0,0,40,0,0,0
  //   ,d,f,0,40,40,d,0,d,0,f,7*0,f,0,0,40,4*0,f,0,40,0,d,0,d,0,f,0,40
  //   ,0,d,0,d,0,f,7*0,f,10*0,6,15*0,6,15*0,6,151*0,2,0,0,0,80,11*0
  //   ,4,0,0,0,80,11*0,7,0,0,0,80,27*0,2,7*0,1,7*0,4,7*0,1,7*0,7,9,6*0
  //   ,1,9,6*0,b,9,7*0,9,133*0,40,40,0,0,f,0,1,0,0,40,0,0,0,f,1,0,40,40
  //   ,0,0,f,0,1,7*0,1,0,0,40,4*0,1,0,40,0,0,0,f,0,1,0,40,0,0,0,f,0
  //   ,1,18*0,f,15*0,f,15*0,f,223*0,7,15*0,7,15*0,7,6,15*0,1,137*0,80
  //   ,8*0,80,6*0,80,23*0,80,7*0,80,309*0,7,153*0,80,8*0,80,6*0,80,23*0
  //   ,80,7*0,80,1803*0,c,c,c,0,0,0,c,c,0,c,c,0,0,0,c,c,0,c,c,0,0,0
  //   ,c,c,0,c,c,0,0,0,c,c,0,c,c,0,0,0,c,0,0,c,c,0,0,0,c,c,0,c,c,0,0,0
  //   ,c,0,0,0,c,0,0,0,c,0,0,8*c,0,8*c,0,8*c,0,8*c,0,26*c,0,71*c,0,c,c,c
  //   ,0,c,c,c,0,c,c,c,0,c,c,c,0,c,0,c,0,c,0,c,0,c,c,c,0,c,c,c,0,c,0
  //   ,c,0,c,0,c,0,c,0,c,0,c,0,c,0,c,0,c,0,c,0,c,10*0,1,1,4*0,1,9*0
  //   ,1,1,4*0,1,9*0,1,5*0,1,17*0,7*2,3,0,6*3,4,4,0,5*4,5,5,5,0,4*5
  //   ,4*6,0,6,6,6,5*7,e,7,7,8*0,7*1,0,64*f,0,3,0,0,0,80,11*0,5,0,0,0
  //   ,80,11*0,6,0,0,0,80,27*0,3,4*0,2,1,0,f,4*0,3,0,0,5,4*0,4,1,0,f
  //   ,4*0,5,0,0,6,8,0,0,0,6,0,0,f,8,0,0,0,7,0,0,a,8,0,0,0,d,0,0,0,8
  //   ,0,0,0,1,65*0,56*1,8*0,40,40,d,d,d,0,f,0,0,40,0,0,0,d,f,0,40,40
  //   ,d,0,d,0,f,7*0,f,0,40,40,d,0,d,0,f,7*0,f,7*0,f,0,40,0,d,0,d,0
  //   ,f,10*0,6,15*0,6,15*0,6,151*0,2,0,0,0,80,11*0,4,0,0,0,80,11*0
  //   ,7,0,0,0,80,27*0,2,7*0,1,7*0,4,7*0,1,7*0,7,9,6*0,1,9,6*0,b,9,7*0
  //   ,9,133*0,40,40,0,0,f,0,1,0,0,40,0,0,0,f,1,0,40,40,0,0,f,0,1,7*0
  //   ,1,0,40,40,0,0,f,0,1,7*0,1,7*0,1,0,40,0,0,0,f,12*0,f,15*0,f,15*0
  //   ,f,223*0,7,15*0,7,15*0,7,6,15*0,1,137*0,80,8*0,80,6*0,80,15*0
  //   ,80,23*0,80,301*0,7,153*0,80,8*0,80,6*0,80,15*0,80,23*0,80,1795*0
  //   ,c,c,c,0,0,0,c,c,0,c,c,0,0,0,c,c,0,c,c,0,0,0,c,c,0,c,c,0,0,0,c,c
  //   ,0,c,c,0,0,0,c,0,0,c,c,0,0,0,c,c,0,c,c,0,0,0,c,0,0,0,c,0,0,0,c
  //   ,0,0,8*c,0,8*c,0,8*c,0,8*c,0,26*c,0,71*c,0,c,c,c,0,c,c,c,0,c,c,c
  //   ,0,c,c,c,0,c,0,c,0,c,0,c,0,c,c,c,0,c,c,c,0,c,0,c,0,c,0,c,0,c,0
  //   ,c,0,c,0,c,0,c,0,c,0,c,0,c,10*0,1,1,4*0,1,9*0,1,1,4*0,1,9*0,1
  //   ,5*0,1,17*0,7*2,3,0,6*3,4,4,0,5*4,5,5,5,0,4*5,4*6,0,6,6,6,5*7
  //   ,e,7,7,8*0,7*1,0,64*f,0,3,0,0,0,80,11*0,5,0,0,0,80,11*0,6,0,0,0
  //   ,80,27*0,3,4*0,2,1,0,f,4*0,3,0,0,5,4*0,4,1,0,f,4*0,5,0,0,6,8,0,0,0
  //   ,6,0,0,f,8,0,0,0,7,0,0,a,8,0,0,0,d,0,0,0,8,0,0,0,1,65*0,56*1,8*0
  //   ,40,40,d,d,d,0,f,0,0,40,0,0,0,d,f,0,40,40,d,0,d,0,f,7*0,f,0,0
  //   ,40,4*0,f,0,40,0,d,0,d,0,f,7*0,f,0,40,0,d,0,d,0,f,10*0,6,15*0
  //   ,6,15*0,6,151*0,2,0,0,0,80,11*0,4,0,0,0,80,11*0,7,0,0,0,80,27*0
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  //   contents of eeprom_3 (hex, n*v repeats v):
  //   263*0,2c,7*0,20,7*0,2c,7*0,20,15*0,10,144*0,40,8*0,40,6*0,40,15*0
  //   ,40,15*0,40,22*0,c,120*0,16*29,16*26,8*3b,8*39,8*3b,8*26,73*0
  //   ,29,15*0,29,15*0,29,150*0,80,8*0,80,6*0,80,15*0,80,15*0,80,209*0
  //   ,80,80,0,0,29,7*0,29,0,0,0,80,0,0,0,26,7*0,26,0,0,0,80,0,0,0,3b
  //   ,7*0,39,0,0,0,80,0,0,0,3b,7*0,26,195*0,40,40,14*0,40,15*0,40,15*0
  //   ,40,22*0,29,15*0,29,15*0,29,1178*0,9a,8*0,9a,6*0,9a,15*0,9a,15*0
  //   ,9a,207*0,40,8*0,40,6*0,40,15*0,40,15*0,40,1298*0,2c,7*0,20,7*0
  //   ,2c,7*0,20,15*0,10,144*0,40,8*0,40,6*0,40,23*0,40,7*0,40,22*0
  //   ,c,120*0,16*29,16*26,8*3b,8*39,8*3b,8*26,73*0,29,15*0,29,15*0
  //   ,29,150*0,80,8*0,80,6*0,80,23*0,80,7*0,80,209*0,80,80,0,0,29,7*0
  //   ,29,0,0,0,80,0,0,0,26,7*0,26,7*0,3b,0,0,0,80,0,0,0,39,0,0,0,80
  //   ,0,0,0,3b,7*0,26,195*0,40,40,14*0,40,23*0,40,7*0,40,22*0,29,15*0
  //   ,29,15*0,29,1178*0,9a,8*0,9a,6*0,9a,23*0,9a,7*0,9a,207*0,40,8*0
  //   ,40,6*0,40,23*0,40,7*0,40,1298*0,2c,7*0,20,7*0,2c,7*0,20,15*0
  //   ,10,144*0,40,8*0,40,6*0,40,15*0,40,23*0,40,14*0,c,120*0,16*29
  //   ,16*26,8*3b,8*39,8*3b,8*26,73*0,29,15*0,29,15*0,29,150*0,80,8*0
  //   ,80,6*0,80,15*0,80,23*0,80,201*0,80,80,0,0,29,7*0,29,0,0,0,80
  //   ,0,0,0,26,7*0,26,0,0,0,80,0,0,0,3b,7*0,39,7*0,3b,0,0,0,80,0,0,0
  //   ,26,195*0,40,40,14*0,40,15*0,40,23*0,40,14*0,29,15*0,29,15*0,29
  //   ,1178*0,9a,8*0,9a,6*0,9a,15*0,9a,23*0,9a,199*0,40,8*0,40,6*0,40
  //   ,15*0,40,23*0,40,1290*0,2c,7*0,20,7*0,2c,7*0,20,15*0,10,144*0
  //   ,40,8*0,40,6*0,40,23*0,40,15*0,40,14*0,c,120*0,16*29,16*26,8*3b
  //   ,8*39,8*3b,8*26,73*0,29,15*0,29,15*0,29,150*0,80,8*0,80,6*0,80
  //   ,23*0,80,15*0,80,201*0,80,80,0,0,29,7*0,29,0,0,0,80,0,0,0,26,7*0
  //   ,26,7*0,3b,0,0,0,80,0,0,0,39,7*0,3b,0,0,0,80,0,0,0,26,195*0,40,40
  //   ,14*0,40,23*0,40,15*0,40,14*0,29,15*0,29,15*0,29,1178*0,9a,8*0
  //   ,9a,6*0,9a,23*0,9a,15*0,9a,199*0,40,8*0,40,6*0,40,23*0,40,15*0
  //   ,40,1290*0,2c,7*0,20,7*0,2c,7*0,20,15*0,10,144*0,40,8*0,40,14*0
  //   ,40,7*0,40,15*0,40,22*0,c,120*0,16*29,16*26,8*3b,8*39,8*3b,8*26
  //   ,73*0,29,15*0,29,15*0,29,150*0,80,8*0,80,14*0,80,7*0,80,15*0,80
  //   ,209*0,80,80,0,0,29,7*0,29,7*0,26,0,0,0,80,0,0,0,26,0,0,0,80,0,0,0
  //   ,3b,7*0,39,0,0,0,80,0,0,0,3b,7*0,26,195*0,40,40,22*0,40,7*0,40
  //   ,15*0,40,22*0,29,15*0,29,15*0,29,1178*0,9a,8*0,9a,14*0,9a,7*0
  //   ,9a,15*0,9a,207*0,40,8*0,40,14*0,40,7*0,40,15*0,40,1298*0,2c,7*0
  //   ,20,7*0,2c,7*0,20,15*0,10,144*0,40,8*0,40,14*0,40,15*0,40,7*0
  //   ,40,22*0,c,120*0,16*29,16*26,8*3b,8*39,8*3b,8*26,73*0,29,15*0
  //   ,29,15*0,29,150*0,80,8*0,80,14*0,80,15*0,80,7*0,80,209*0,80,80
  //   ,0,0,29,7*0,29,7*0,26,0,0,0,80,0,0,0,26,7*0,3b,0,0,0,80,0,0,0
  //   ,39,0,0,0,80,0,0,0,3b,7*0,26,195*0,40,40,22*0,40,15*0,40,7*0,40
  //   ,22*0,29,15*0,29,15*0,29,1178*0,9a,8*0,9a,14*0,9a,15*0,9a,7*0
  //   ,9a,207*0,40,8*0,40,14*0,40,15*0,40,7*0,40,1298*0,2c,7*0,20,7*0
  //   ,2c,7*0,20,15*0,10,144*0,40,8*0,40,14*0,40,7*0,40,23*0,40,14*0
  //   ,c,120*0,16*29,16*26,8*3b,8*39,8*3b,8*26,73*0,29,15*0,29,15*0
  //   ,29,150*0,80,8*0,80,14*0,80,7*0,80,23*0,80,201*0,80,80,0,0,29
  //   ,7*0,29,7*0,26,0,0,0,80,0,0,0,26,0,0,0,80,0,0,0,3b,7*0,39,7*0
  //   ,3b,0,0,0,80,0,0,0,26,195*0,40,40,22*0,40,7*0,40,23*0,40,14*0
  //   ,29,15*0,29,15*0,29,1178*0,9a,8*0,9a,14*0,9a,7*0,9a,23*0,9a,199*0
  //   ,40,8*0,40,14*0,40,7*0,40,23*0,40,1290*0,2c,7*0,20,7*0,2c,7*0
  //   ,20,15*0,10,144*0,40,8*0,40,14*0,40,15*0,40,15*0,40,14*0,c,120*0
  //   ,16*29,16*26,8*3b,8*39,8*3b,8*26,73*0,29,15*0,29,15*0,29,150*0
  //   ,80,8*0,80,14*0,80,15*0,80,15*0,80,201*0,80,80,0,0,29,7*0,29,7*0
  //   ,26,0,0,0,80,0,0,0,26,7*0,3b,0,0,0,80,0,0,0,39,7*0,3b,0,0,0,80
  //   ,0,0,0,26,195*0,40,40,22*0,40,15*0,40,15*0,40,14*0,29,15*0,29
  //   ,15*0,29,1178*0,9a,8*0,9a,14*0,9a,15*0,9a,15*0,9a,199*0,40,8*0
  //   ,40,14*0,40,15*0,40,15*0,40,1290*0,2c,7*0,20,7*0,2c,7*0,20,15*0
  //   ,10,152*0,40,40,6*0,40,15*0,40,15*0,40,22*0,c,120*0,16*29,16*26
  //   ,8*3b,8*39,8*3b,8*26,73*0,29,15*0,29,15*0,29,158*0,80,80,6*0,80
  //   ,15*0,80,15*0,80,210*0,80,0,0,29,0,0,0,80,0,0,0,29,0,0,0,80,0,0,0
  //   ,26,7*0,26,0,0,0,80,0,0,0,3b,7*0,39,0,0,0,80,0,0,0,3b,7*0,26,196*0
  //   ,40,6*0,40,7*0,40,15*0,40,15*0,40,22*0,29,15*0,29,15*0,29,1186*0
  //   ,9a,9a,6*0,9a,15*0,9a,15*0,9a,215*0,40,40,6*0,40,15*0,40,15*0
  //   ,40,1298*0,2c,7*0,20,7*0,2c,7*0,20,15*0,10,152*0,40,40,6*0,40
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  //   contents of eeprom_4 (hex, n*v repeats v):
  //   0,0,0,22,22,22,0,0,22,0,0,22,22,22,0,0,22,0,0,22,22,22,0,0,22
  //   ,0,0,22,22,22,0,0,22,0,0,22,22,22,0,22,22,0,0,22,22,22,0,0,22
  //   ,0,0,22,22,22,0,22,22,22,0,22,22,22,0,22,22,8*0,22,8*0,22,8*0
  //   ,22,8*0,22,26*0,22,71*0,22,0,0,0,22,0,0,0,22,0,0,0,22,0,0,0,22
  //   ,0,22,0,22,0,22,0,22,0,0,0,22,0,0,0,22,0,22,0,22,0,22,0,22,0,22
  //   ,0,22,0,22,0,22,0,22,0,22,0,22,0,22,23,1,27,22,22,22,1,1,22,1
  //   ,23,22,22,22,1,23,22,1,27,22,22,22,1,1,22,1,23,22,22,22,1,23,22
  //   ,1,1,22,22,22,1,22,22,1,1,22,22,22,1,23,22,1,1,22,22,22,1,22,22,22
  //   ,1,22,22,22,1,22,22,8*23,22,8*23,22,8*23,22,8*23,22,11*23,6*27
  //   ,23,27,7*23,22,64*1,0,6*1,22,23,0,1,22,1,1,1,22,0,1,1,22,1,1,1
  //   ,22,23,22,1,22,1,22,1,22,0,1,1,22,1,1,1,22,23,22,1,22,1,22,1,22
  //   ,0,22,1,22,1,22,1,22,23,22,1,22,1,22,1,22,22,0,4*22,0,22,22,0
  //   ,4*22,0,22,22,0,4*22,0,22,22,0,4*22,0,22,22,0,0,22,22,22,0,22,22
  //   ,0,0,22,22,22,0,22,22,0,0,22,22,22,0,22,22,22,0,22,22,22,0,129*22
  //   ,5*0,4,0,22,22,0,1,22,1,0,0,22,0,0,0,22,0,4,0,22,22,22,1,22,1
  //   ,22,0,22,0,0,0,22,0,4,0,22,22,22,1,22,1,22,0,22,0,22,0,22,0,22
  //   ,0,22,22,22,1,22,1,22,0,22,22,1,4*22,23,22,22,0,4*22,23,22,22
  //   ,1,4*22,23,22,22,0,4*22,23,22,22,1,1,22,22,22,23,22,22,0,1,22,22,22
  //   ,23,22,22,1,1,22,22,22,1,22,22,22,1,22,22,22,23,129*22,0,0,1,1,1
  //   ,0,1,22,22,0,23,22,23,1,1,22,0,0,1,22,1,0,1,22,22,22,23,22,23
  //   ,22,1,22,0,0,1,22,1,0,1,22,22,22,23,22,23,22,1,22,0,22,1,22,1
  //   ,22,1,22,22,22,23,22,23,22,1,22,22,0,7*22,0,7*22,0,7*22,0,7*22
  //   ,0,0,6*22,0,0,6*22,0,0,22,22,22,26,22,22,22,0,135*22,0,0,0,26
  //   ,7*22,0,4*22,0,22,0,26,12*22,0,22,0,26,12*22,0,22,0,12*22,23,7*22
  //   ,0,7*22,23,7*22,0,7*22,23,1,6*22,0,1,6*22,23,1,7*22,1,137*22,1
  //   ,8*22,1,6*22,1,15*22,1,15*22,1,20*22,0,15*22,0,8*22,4,6*22,0,0
  //   ,7*22,26,145*22,0,8*22,0,6*22,0,15*22,0,15*22,0,45*22,10,7*22
  //   ,10,153*22,4,8*22,4,6*22,4,15*22,4,15*22,4,45*22,26,161*22,0,8*22
  //   ,0,6*22,0,15*22,0,15*22,0,207*22,4,8*22,4,6*22,4,15*22,4,15*22
  //   ,4,207*22,0,8*22,0,6*22,0,15*22,0,15*22,0,1291*22,0,0,0,22,22,22
  //   ,0,0,22,0,0,22,22,22,0,0,22,0,0,22,22,22,0,0,22,0,0,22,22,22,0,0
  //   ,22,0,0,22,22,22,0,22,22,0,0,22,22,22,0,0,22,0,0,22,22,22,0,22,22,22
  //   ,0,22,22,22,0,22,22,8*0,22,8*0,22,8*0,22,8*0,22,26*0,22,71*0,22
  //   ,0,0,0,22,0,0,0,22,0,0,0,22,0,0,0,22,0,22,0,22,0,22,0,22,0,0,0
  //   ,22,0,0,0,22,0,22,0,22,0,22,0,22,0,22,0,22,0,22,0,22,0,22,0,22
  //   ,0,22,0,22,23,1,27,22,22,22,1,1,22,1,23,22,22,22,1,23,22,1,27
  //   ,22,22,22,1,1,22,1,23,22,22,22,1,23,22,1,1,22,22,22,1,22,22,1,1
  //   ,22,22,22,1,23,22,1,1,22,22,22,1,22,22,22,1,22,22,22,1,22,22,8*23
  //   ,22,8*23,22,8*23,22,8*23,22,11*23,6*27,23,27,7*23,22,64*1,0,6*1
  //   ,22,23,0,1,22,1,1,1,22,0,1,1,22,1,1,1,22,23,22,1,22,1,22,1,22
  //   ,23,1,1,22,1,1,1,22,0,22,1,22,1,22,1,22,0,22,1,22,1,22,1,22,23
  //   ,22,1,22,1,22,1,22,22,0,4*22,0,22,22,0,4*22,0,22,22,0,4*22,0,22,22
  //   ,0,4*22,0,22,22,0,0,22,22,22,0,22,22,0,0,22,22,22,0,22,22,0,0
  //   ,22,22,22,0,22,22,22,0,22,22,22,0,129*22,5*0,4,0,22,22,0,1,22
  //   ,1,0,0,22,0,0,0,22,0,4,0,22,22,22,1,22,1,22,0,22,22,0,1,22,1,4
  //   ,0,22,0,22,0,22,0,22,0,22,0,22,0,22,0,22,0,22,22,22,1,22,1,22
  //   ,0,22,22,1,4*22,23,22,22,0,4*22,23,22,22,1,4*22,23,22,22,0,4*22
  //   ,23,22,22,1,1,22,22,22,23,22,22,0,1,22,22,22,23,22,22,1,1,22,22,22
  //   ,1,22,22,22,1,22,22,22,23,129*22,0,0,1,1,1,0,1,22,22,0,23,22,23
  //   ,1,1,22,0,0,1,22,1,0,1,22,22,22,23,22,23,22,1,22,22,0,23,22,23
  //   ,0,1,22,0,22,1,22,1,22,1,22,0,22,1,22,1,22,1,22,22,22,23,22,23
  //   ,22,1,22,22,0,7*22,0,7*22,0,7*22,0,7*22,0,0,6*22,0,0,6*22,0,0
  //   ,22,22,22,26,22,22,22,0,135*22,0,0,0,26,7*22,0,4*22,0,22,0,26
  //   ,15*22,26,4*22,0,22,0,5*22,0,22,0,12*22,23,7*22,0,7*22,23,7*22
  //   ,0,7*22,23,1,6*22,0,1,6*22,23,1,7*22,1,137*22,1,8*22,1,6*22,1
  //   ,23*22,1,7*22,1,20*22,0,15*22,0,8*22,4,6*22,0,0,7*22,26,145*22
  //   ,0,8*22,0,6*22,0,23*22,0,7*22,0,45*22,10,7*22,10,153*22,4,8*22
  //   ,4,6*22,4,23*22,4,7*22,4,45*22,26,161*22,0,8*22,0,6*22,0,23*22
  //   ,0,7*22,0,207*22,4,8*22,4,6*22,4,23*22,4,7*22,4,207*22,0,8*22
  //   ,0,6*22,0,23*22,0,7*22,0,1291*22,0,0,0,22,22,22,0,0,22,0,0,22,22,22
  //   ,0,0,22,0,0,22,22,22,0,0,22,0,0,22,22,22,0,0,22,0,0,22,22,22,0
  //   ,22,22,0,0,22,22,22,0,0,22,0,0,22,22,22,0,22,22,22,0,22,22,22
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endmodule
