// Digital circuit main.dig as structural Verilog
module main (
  input  PROG,
  input  L_nH,
  input  [7:0] MAR_DATAIN,
  input  [7:0] ROM_DATAIN,
  input  PROG_ROM,
  input  CLK_DISP,
  input  MAR_LIN,
  input  MAR_HIN,
  input  nMAR_OUT,
  input  ALU_S0,
  input  ALU_S1,
  input  ALU_S2,
  input  ALU_S3,
  input  ALU_M,
  input  ALU_BIN,
  input  nALU_OUT,
  input  FR_IN,
  input  SP_LIN,
  input  SP_HIN,
  input  nSP_OUT,
  input  nINC_SP,
  input  nDEC_SP,
  input  PC_E,
  input  nJMP_L,
  input  nJMP_H,
  input  nPC_HLOUT,
  input  RAM_IN,
  input  RAM_OUT,
  input  SC_RST,
  input  IR_IN,
  input  REG_OUTIN,
  input  REG_AIN,
  input  nREG_AOUT,
  input  REG_BIN,
  input  REG_CIN,
  input  nREG_BOUT,
  input  nREG_COUT,
  input  nPAIR_BCOUT,
  input  nINC_H,
  input  nDEC_H,
  input  REG_LIN,
  input  REG_HIN,
  input  nREG_LOUT,
  input  nREG_HOUT,
  input  nPAIR_HLOUT,
  input  RST,
  input  REG_DIN,
  input  nREG_DOUT,
  input  REG_EIN,
  input  nREG_EOUT,
  input  nPAIR_DEOUT,
  input  VCC,
  input  GND,
  input  CLK,
  input  HLT,
  input  [7:0] RAM_DATAIN
);

  wire address_decoder_1_nram_cs, address_decoder_1_nrom_cs, CLK_t, nALU_OUT_t, nDEC_H_t, nDEC_SP_t,
       nINC_H_t, nINC_SP_t, nJMP_H_t, nJMP_L_t, nMAR_OUT_t, not_1_out, nPAIR_BCOUT_t, nPAIR_DEOUT_t,
       nPAIR_HLOUT_t, nPC_HLOUT_t, nREG_AOUT_t, nREG_BOUT_t, nREG_COUT_t, nREG_DOUT_t, nREG_EOUT_t,
       nREG_HOUT_t, nREG_LOUT_t, nRST, nSP_OUT_t, step_counter_1_step_0, step_counter_1_step_1,
       step_counter_1_step_2, step_counter_1_step_3;
  wire [3:0] undriven_2;
  wire [7:0] mar_1_mar_hint, mar_1_mar_lint, ram_1_ram_int, register_d_e_1_p10, register_d_e_1_p12,
       register_d_e_1_p13, register_instruction_1_ir_bus, rom_1_bus, rom_1_rom_int, undriven, undriven_3,
       undriven_4, undriven_5;
  wire [11:0] register_output_1_led_segout;
  wire [15:0] mar_1_addr_bus, program_counter_1_pc_int, register_h_l_1_reg_hlint, stack_pointer_1_sp_int;

  LED led_1 (.in(mar_1_mar_hint[7]));
  LED led_2 (.in(mar_1_mar_hint[6]));
  LED led_3 (.in(stack_pointer_1_sp_int[14]));
  LED led_4 (.in(stack_pointer_1_sp_int[15]));
  LED led_5 (.in(program_counter_1_pc_int[14]));
  LED led_6 (.in(program_counter_1_pc_int[15]));
  LED led_7 (.in(mar_1_mar_hint[5]));
  LED led_8 (.in(mar_1_mar_hint[4]));
  LED led_9 (.in(stack_pointer_1_sp_int[12]));
  LED led_10 (.in(stack_pointer_1_sp_int[13]));
  LED led_11 (.in(program_counter_1_pc_int[12]));
  LED led_12 (.in(program_counter_1_pc_int[13]));
  LED led_13 (.in(mar_1_mar_hint[3]));
  LED led_14 (.in(mar_1_mar_hint[2]));
  LED led_15 (.in(stack_pointer_1_sp_int[10]));
  LED led_16 (.in(stack_pointer_1_sp_int[11]));
  LED led_17 (.in(program_counter_1_pc_int[10]));
  LED led_18 (.in(program_counter_1_pc_int[11]));
  LED led_19 (.in(mar_1_mar_hint[1]));
  LED led_20 (.in(mar_1_mar_hint[0]));
  LED led_21 (.in(stack_pointer_1_sp_int[8]));
  LED led_22 (.in(stack_pointer_1_sp_int[9]));
  LED led_23 (.in(program_counter_1_pc_int[8]));
  LED led_24 (.in(program_counter_1_pc_int[9]));
  LED led_25 (.in(mar_1_mar_lint[7]));
  LED led_26 (.in(mar_1_mar_lint[6]));
  LED led_27 (.in(stack_pointer_1_sp_int[6]));
  LED led_28 (.in(stack_pointer_1_sp_int[7]));
  LED led_29 (.in(program_counter_1_pc_int[6]));
  LED led_30 (.in(program_counter_1_pc_int[7]));
  LED led_31 (.in(ram_1_ram_int[7]));
  LED led_32 (.in(ram_1_ram_int[6]));
  LED led_33 (.in(rom_1_rom_int[7]));
  LED led_34 (.in(rom_1_rom_int[6]));
  LED led_35 (.in(mar_1_mar_lint[5]));
  LED led_36 (.in(mar_1_mar_lint[4]));
  LED led_37 (.in(stack_pointer_1_sp_int[4]));
  LED led_38 (.in(stack_pointer_1_sp_int[5]));
  LED led_39 (.in(program_counter_1_pc_int[4]));
  LED led_40 (.in(program_counter_1_pc_int[5]));
  LED led_41 (.in(ram_1_ram_int[5]));
  LED led_42 (.in(ram_1_ram_int[4]));
  LED led_43 (.in(rom_1_rom_int[5]));
  LED led_44 (.in(rom_1_rom_int[4]));
  LED led_45 (.in(mar_1_addr_bus[14]));
  LED led_46 (.in(mar_1_addr_bus[15]));
  LED led_47 (.in(mar_1_mar_lint[3]));
  LED led_48 (.in(mar_1_mar_lint[2]));
  LED led_49 (.in(stack_pointer_1_sp_int[2]));
  LED led_50 (.in(stack_pointer_1_sp_int[3]));
  LED led_51 (.in(program_counter_1_pc_int[2]));
  LED led_52 (.in(program_counter_1_pc_int[3]));
  LED led_53 (.in(ram_1_ram_int[3]));
  LED led_54 (.in(ram_1_ram_int[2]));
  LED led_55 (.in(rom_1_rom_int[3]));
  LED led_56 (.in(rom_1_rom_int[2]));
  LED led_57 (.in(mar_1_addr_bus[12]));
  LED led_58 (.in(mar_1_addr_bus[13]));
  LED led_59 (.in(mar_1_mar_lint[1]));
  LED led_60 (.in(mar_1_mar_lint[0]));
  LED led_61 (.in(stack_pointer_1_sp_int[0]));
  LED led_62 (.in(stack_pointer_1_sp_int[1]));
  LED led_63 (.in(program_counter_1_pc_int[0]));
  LED led_64 (.in(program_counter_1_pc_int[1]));
  LED led_65 (.in(ram_1_ram_int[1]));
  LED led_66 (.in(ram_1_ram_int[0]));
  LED led_67 (.in(rom_1_rom_int[1]));
  LED led_68 (.in(rom_1_rom_int[0]));
  LED led_69 (.in(mar_1_addr_bus[10]));
  LED led_70 (.in(mar_1_addr_bus[11]));
  LED led_71 (.in(mar_1_addr_bus[8]));
  LED led_72 (.in(mar_1_addr_bus[9]));
  LED led_73 (.in(mar_1_addr_bus[6]));
  LED led_74 (.in(mar_1_addr_bus[7]));
  LED led_75 (.in(mar_1_addr_bus[4]));
  LED led_76 (.in(mar_1_addr_bus[5]));
  mar mar_1 (
    .nMAR_OUT(nMAR_OUT_t), .MAR_LIN(MAR_LIN), .MAR_HIN(MAR_HIN), .CLK(CLK_t), .VCC(VCC), .GND(GND),
    .BUS(rom_1_bus), .MAR_DATAIN(MAR_DATAIN), .PROG(PROG), .L_nH(L_nH), .ADDR_BUS(mar_1_addr_bus),
    .MAR_LINT(mar_1_mar_lint), .MAR_HINT(mar_1_mar_hint));
  stack_pointer stack_pointer_1 (
    .BUS(rom_1_bus), .nDEC_SP(nDEC_SP_t), .SP_LIN(SP_LIN), .SP_HIN(SP_HIN), .RST(RST), .VCC(VCC), .GND(GND),
    .nSP_OUT(nSP_OUT_t), .nINC_SP(nINC_SP_t), .CLK(CLK_t), .ADDR_BUS(mar_1_addr_bus),
    .SP_INT(stack_pointer_1_sp_int));
  program_counter program_counter_1 (
    .nPC_HLOUT(nPC_HLOUT_t), .BUS(rom_1_bus), .VCC(VCC), .GND(GND), .PC_E(PC_E), .nJMP_L(nJMP_L_t),
    .nJMP_H(nJMP_H_t), .CLK(CLK_t), .nRST(nRST), .ADDR_BUS(mar_1_addr_bus), .PC_INT(program_counter_1_pc_int));  // open: nPC_LOUT, nPC_HOUT
  address_decoder address_decoder_1 (
    .ADDR_BUS(mar_1_addr_bus), .RAM_IN(RAM_IN), .VCC(VCC), .GND(GND), .nRAM_CS(address_decoder_1_nram_cs),
    .nROM_CS(address_decoder_1_nrom_cs));  // open: nCF_CS, LCD_RS, LCD_E
  ram ram_1 (
    .VCC(VCC), .GND(GND), .RAM_DATAIN(RAM_DATAIN), .ADDR_BUS(mar_1_addr_bus), .RAM_OUT(RAM_OUT), .PROG(PROG),
    .RAM_IN(RAM_IN), .CLK(CLK_t), .BUS(rom_1_bus), .nRAM_CS(address_decoder_1_nram_cs),
    .RAM_INT(ram_1_ram_int));
  rom rom_1 (
    .nROM_CS(address_decoder_1_nrom_cs), .VCC(VCC), .GND(GND), .ROM_DATAIN(ROM_DATAIN), .PROG_ROM(PROG_ROM),
    .ADDR_BUS(mar_1_addr_bus), .BUS(rom_1_bus), .ROM_INT(rom_1_rom_int));
  LED led_77 (.in(mar_1_addr_bus[2]));
  LED led_78 (.in(mar_1_addr_bus[3]));
  LED led_79 (.in(mar_1_addr_bus[0]));
  LED led_80 (.in(mar_1_addr_bus[1]));
  LED led_81 (.in(rom_1_bus[7]));
  LED led_82 (.in(rom_1_bus[6]));
  LED led_83 (.in(rom_1_bus[5]));
  LED led_84 (.in(rom_1_bus[4]));
  LED led_85 (.in(rom_1_bus[3]));
  not not_1 (not_1_out, CLK_t);
  LED led_86 (.in(rom_1_bus[2]));
  LED led_87 (.in(rom_1_bus[1]));
  LED led_88 (.in(rom_1_bus[0]));
  register_a register_a_1 (
    .VCC(VCC), .GND(GND), .REG_AIN(REG_AIN), .CLK(CLK_t), .nREG_AOUT(nREG_AOUT_t), .BUS(rom_1_bus));  // open: REG_AINT
  alu alu_1 (
    .BUS(rom_1_bus), .REG_AINT(undriven_4), .ALU_S3(ALU_S3), .ALU_S2(ALU_S2), .ALU_S1(ALU_S1),
    .ALU_S0(ALU_S0), .ALU_M(ALU_M), .nALU_OUT(nALU_OUT_t), .VCC(VCC), .GND(GND), .clk(CLK_t),
    .ALU_BIN(ALU_BIN), .FR_IN(FR_IN));  // open: ZF, CF, NF, VF
  register_b_c register_b_c_1 (
    .REG_BIN(REG_BIN), .clk(CLK_t), .REG_CI(REG_CIN), .VCC(VCC), .GND(GND), .BUS(rom_1_bus),
    .nREG_BOUT(nREG_BOUT_t), .nREG_COUT(nREG_COUT_t), .nPAIR_BCOUT(nPAIR_BCOUT_t));  // open: ADDR_BUS
  // register_d_e register_d_e_1: pin names not known; wires that end beside it: REG_DIN, CLK_t, REG_EIN, VCC, GND, rom_1_bus, nREG_DOUT_t, nREG_EOUT_t, nPAIR_DEOUT_t, register_d_e_1_p10, mar_1_addr_bus, register_d_e_1_p12, register_d_e_1_p13
  register_h_l register_h_l_1 (
    .BUS(rom_1_bus), .nDEC_H(nDEC_H_t), .REG_LIN(REG_LIN), .REG_HIN(REG_HIN), .RST(RST), .VCC(VCC),
    .GND(GND), .nREG_LOUT(nREG_LOUT_t), .nREG_HOUT(nREG_HOUT_t), .nPAIR_HLOUT(nPAIR_HLOUT_t),
    .nINC_H(nINC_H_t), .CLK(CLK_t), .ADDR_BUS(mar_1_addr_bus), .REG_HLINT(register_h_l_1_reg_hlint));
  register_output register_output_1 (
    .CLK(CLK_t), .REG_OUTIN(REG_OUTIN), .CLK_DISP(CLK_DISP), .BUS(rom_1_bus), .VCC(VCC), .GND(GND),
    .LED_SEGOUT(register_output_1_led_segout));
  step_counter step_counter_1 (
    .nCLK(not_1_out), .VCC(VCC), .GND(GND), .SC_RST(SC_RST), .RST(RST), .STEP_0(step_counter_1_step_0),
    .STEP_1(step_counter_1_step_1), .STEP_2(step_counter_1_step_2), .STEP_3(step_counter_1_step_3));  // open: CLR
  register_instruction register_instruction_1 (
    .BUS(rom_1_bus), .CLK(CLK_t), .IR_IN(IR_IN), .VCC(VCC), .GND(GND), .IR_BUS(register_instruction_1_ir_bus));
  LED led_89 (.in(undriven_4[7]));
  LED led_90 (.in(undriven_4[6]));
  LED led_91 (.in(undriven_5[7]));
  LED led_92 (.in(undriven_5[6]));
  LED led_93 (.in(undriven[7]));
  LED led_94 (.in(undriven[6]));
  LED led_95 (.in(undriven_2[0]));
  LED led_96 (.in(undriven_2[1]));
  LED led_97 (.in(undriven_3[7]));
  LED led_98 (.in(undriven_3[6]));
  LED led_99 (.in(register_d_e_1_p10[7]));
  LED led_100 (.in(register_d_e_1_p10[6]));
  LED led_101 (.in(register_d_e_1_p12[7]));
  LED led_102 (.in(register_d_e_1_p12[6]));
  LED led_103 (.in(register_d_e_1_p13[7]));
  LED led_104 (.in(register_d_e_1_p13[6]));
  LED led_105 (.in(register_h_l_1_reg_hlint[14]));
  LED led_106 (.in(register_h_l_1_reg_hlint[15]));
  LED led_107 (.in(step_counter_1_step_2));
  LED led_108 (.in(step_counter_1_step_3));
  LED led_109 (.in(register_instruction_1_ir_bus[7]));
  LED led_110 (.in(register_instruction_1_ir_bus[6]));
  LED led_111 (.in(undriven_4[5]));
  LED led_112 (.in(undriven_4[4]));
  LED led_113 (.in(undriven_5[5]));
  LED led_114 (.in(undriven_5[4]));
  LED led_115 (.in(undriven[5]));
  LED led_116 (.in(undriven[4]));
  LED led_117 (.in(undriven_2[2]));
  LED led_118 (.in(undriven_2[3]));
  LED led_119 (.in(undriven_3[5]));
  LED led_120 (.in(undriven_3[4]));
  LED led_121 (.in(register_d_e_1_p10[5]));
  LED led_122 (.in(register_d_e_1_p10[4]));
  LED led_123 (.in(register_d_e_1_p12[5]));
  LED led_124 (.in(register_d_e_1_p12[4]));
  LED led_125 (.in(register_d_e_1_p13[5]));
  LED led_126 (.in(register_d_e_1_p13[4]));
  LED led_127 (.in(register_h_l_1_reg_hlint[12]));
  LED led_128 (.in(register_h_l_1_reg_hlint[13]));
  LED led_129 (.in(step_counter_1_step_0));
  LED led_130 (.in(step_counter_1_step_1));
  LED led_131 (.in(register_instruction_1_ir_bus[5]));
  LED led_132 (.in(register_instruction_1_ir_bus[4]));
  LED led_133 (.in(undriven_4[3]));
  LED led_134 (.in(undriven_4[2]));
  LED led_135 (.in(undriven_5[3]));
  LED led_136 (.in(undriven_5[2]));
  LED led_137 (.in(undriven[3]));
  LED led_138 (.in(undriven[2]));
  LED led_139 (.in(undriven_3[3]));
  LED led_140 (.in(undriven_3[2]));
  LED led_141 (.in(register_d_e_1_p10[3]));
  LED led_142 (.in(register_d_e_1_p10[2]));
  LED led_143 (.in(register_d_e_1_p12[3]));
  LED led_144 (.in(register_d_e_1_p12[2]));
  LED led_145 (.in(register_d_e_1_p13[3]));
  LED led_146 (.in(register_d_e_1_p13[2]));
  LED led_147 (.in(register_h_l_1_reg_hlint[10]));
  LED led_148 (.in(register_h_l_1_reg_hlint[11]));
  LED led_149 (.in(register_instruction_1_ir_bus[3]));
  LED led_150 (.in(register_instruction_1_ir_bus[2]));
  LED led_151 (.in(undriven_4[1]));
  LED led_152 (.in(undriven_4[0]));
  LED led_153 (.in(undriven_5[1]));
  LED led_154 (.in(undriven_5[0]));
  LED led_155 (.in(undriven[1]));
  LED led_156 (.in(undriven[0]));
  LED led_157 (.in(undriven_3[1]));
  LED led_158 (.in(undriven_3[0]));
  LED led_159 (.in(register_d_e_1_p10[1]));
  LED led_160 (.in(register_d_e_1_p10[0]));
  LED led_161 (.in(register_d_e_1_p12[1]));
  LED led_162 (.in(register_d_e_1_p12[0]));
  LED led_163 (.in(register_d_e_1_p13[1]));
  LED led_164 (.in(register_d_e_1_p13[0]));
  LED led_165 (.in(register_h_l_1_reg_hlint[8]));
  LED led_166 (.in(register_h_l_1_reg_hlint[9]));
  Seven_Seg #(.commonCathode("true"), .persistTime(9)) seven_seg_1 (
    .a(register_output_1_led_segout[1]), .b(register_output_1_led_segout[2]),
    .c(register_output_1_led_segout[3]), .d(register_output_1_led_segout[4]),
    .e(register_output_1_led_segout[5]), .f(register_output_1_led_segout[6]),
    .g(register_output_1_led_segout[7]), .dp(register_output_1_led_segout[0]),
    .common(register_output_1_led_segout[8]));
  LED led_167 (.in(register_instruction_1_ir_bus[1]));
  LED led_168 (.in(register_instruction_1_ir_bus[0]));
  LED led_169 (.in(register_h_l_1_reg_hlint[6]));
  LED led_170 (.in(register_h_l_1_reg_hlint[7]));
  Seven_Seg #(.commonCathode("true"), .persistTime(9)) seven_seg_2 (
    .a(register_output_1_led_segout[1]), .b(register_output_1_led_segout[2]),
    .c(register_output_1_led_segout[3]), .d(register_output_1_led_segout[4]),
    .e(register_output_1_led_segout[5]), .f(register_output_1_led_segout[6]),
    .g(register_output_1_led_segout[7]), .dp(register_output_1_led_segout[0]),
    .common(register_output_1_led_segout[9]));
  LED led_171 (.in(register_h_l_1_reg_hlint[4]));
  LED led_172 (.in(register_h_l_1_reg_hlint[5]));
  LED led_173 (.in(register_h_l_1_reg_hlint[2]));
  LED led_174 (.in(register_h_l_1_reg_hlint[3]));
  Seven_Seg #(.commonCathode("true"), .persistTime(9)) seven_seg_3 (
    .a(register_output_1_led_segout[1]), .b(register_output_1_led_segout[2]),
    .c(register_output_1_led_segout[3]), .d(register_output_1_led_segout[4]),
    .e(register_output_1_led_segout[5]), .f(register_output_1_led_segout[6]),
    .g(register_output_1_led_segout[7]), .dp(register_output_1_led_segout[0]),
    .common(register_output_1_led_segout[10]));
  PowerSupply powersupply_1 (.VDD(VCC), .GND(GND));
  not not_2 (nMAR_OUT_t, nMAR_OUT);
  not not_3 (nJMP_L_t, nJMP_L);
  not not_4 (nJMP_H_t, nJMP_H);
  not not_5 (nPC_HLOUT_t, nPC_HLOUT);
  not not_6 (nSP_OUT_t, nSP_OUT);
  not not_7 (nINC_SP_t, nINC_SP);
  not not_8 (nDEC_SP_t, nDEC_SP);
  LED led_175 (.in(register_h_l_1_reg_hlint[0]));
  LED led_176 (.in(register_h_l_1_reg_hlint[1]));
  Seven_Seg #(.commonCathode("true"), .persistTime(9)) seven_seg_4 (
    .a(register_output_1_led_segout[1]), .b(register_output_1_led_segout[2]),
    .c(register_output_1_led_segout[3]), .d(register_output_1_led_segout[4]),
    .e(register_output_1_led_segout[5]), .f(register_output_1_led_segout[6]),
    .g(register_output_1_led_segout[7]), .dp(register_output_1_led_segout[0]),
    .common(register_output_1_led_segout[11]));
  and and_1 (CLK_t, HLT, CLK);
  not not_9 (nRST, RST);
  not not_10 (nALU_OUT_t, nALU_OUT);
  not not_11 (nREG_AOUT_t, nREG_AOUT);
  not not_12 (nREG_BOUT_t, nREG_BOUT);
  not not_13 (nREG_COUT_t, nREG_COUT);
  not not_14 (nPAIR_BCOUT_t, nPAIR_BCOUT);
  not not_15 (nREG_DOUT_t, nREG_DOUT);
  not not_16 (nREG_EOUT_t, nREG_EOUT);
  not not_17 (nPAIR_DEOUT_t, nPAIR_DEOUT);
  not not_18 (nREG_LOUT_t, nREG_LOUT);
  not not_19 (nREG_HOUT_t, nREG_HOUT);
  not not_20 (nPAIR_HLOUT_t, nPAIR_HLOUT);
  not not_21 (nINC_H_t, nINC_H);
  not not_22 (nDEC_H_t, nDEC_H);

  // Notes on the sheet:
  //   CLK_DISP: Hz: 50
  //   VCC: default 1
  //   CLK: Hz: 5
  //   MAR H
  //   Stack pointer
  //   Program counter
  //   RAM output
  //   ROM output
  //   MAR L
  //   Address bus
  //   Bus
  //   V
  //   N
  //   C
  //   Z
  //   Flags
  //   Step
  //   Register pair HL
  //   Register A
  //   ALU buffer
  //   ALU out
  //   Register B
  //   Register C
  //   Register D
  //   Register E
  //   Opcode
endmodule
