// Digital circuit main_manual.dig as structural Verilog
module main_manual (
  input  PROG,
  input  L_nH,
  input  [7:0] MAR_DATAIN,
  input  [7:0] ROM_DATAIN,
  input  PROG_ROM,
  input  RST,
  input  VCC,
  input  GND,
  input  CLK_M,
  input  HLT,
  input  [7:0] RAM_DATAIN,
  input  PROG_RAM,
  input  CLK_DISP,
  input  CLK,
  input  AUTO_EN,
  input  INC_MAR,
  input  [7:0] IR_DATAIN,
  input  IR_SEL
);

  wire address_decoder_1_nram_cs, address_decoder_1_nrom_cs, ALU_BIN, ALU_CARRY, ALU_M, ALU_S0, ALU_S1,
       ALU_S2, ALU_S3, and_1_out, and_2_out, and_3_out, CF, CLK_t, FR_IN, HLT_t, INC_MAR_t, IR_IN, MAR_HIN,
       MAR_LIN, multiplexer_1_out, nALU_OUT, nDEC_H, nDEC_SP, NF, nINC_H, nINC_SP, nJMP_H, nJMP_L, nMAR_OUT,
       not_1_out, not_2_out, not_3_out, not_4_out, not_5_out, not_6_out, not_7_out, not_8_out, not_9_out,
       not_10_out, not_11_out, not_12_out, not_13_out, not_14_out, not_15_out, not_16_out, not_17_out,
       not_18_out, not_19_out, not_20_out, not_21_out, not_22_out, not_23_out, not_24_out, not_25_out,
       not_26_out, not_27_out, nPAIR_BCOUT, nPAIR_DEOUT, nPAIR_HLOUT, nPC_HLOUT, nPC_HOUT, nPC_LOUT,
       nRAR_OUT, nREG_AOUT, nREG_BOUT, nREG_COUT, nREG_DOUT, nREG_EOUT, nREG_HOUT, nREG_LOUT, nREG_TOUT,
       nRRC_OUT, nRST, nSP_OUT, or_1_out, or_2_out, PC_E, RAM_IN, RAM_OUT, REG_AIN, REG_BIN, REG_CIN,
       REG_DIN, REG_EIN, REG_HIN, REG_LIN, REG_OUTIN, REG_TIN, SC_RST, SP_HIN, SP_LIN, STEP_0, STEP_1,
       STEP_2, STEP_3, step_counter_1_clr, VF, ZF;
  wire [3:0] alu_1_flags_int;
  wire [7:0] alu_1_alu_bufint, alu_1_alu_outint, IR_BUS, ram_eeprom_1_ram_int, register_d_e_1_p10,
       register_d_e_1_p12, register_d_e_1_p13, register_instruction_1_ir_bus, register_temporary_1_reg_tint,
       rom_1_bus, rom_1_rom_int, undriven, undriven_2;
  wire [11:0] register_output_1_led_segout;
  wire [15:0] mar_v2_1_addr_bus, mar_v2_1_mar_int, program_counter_1_pc_int, register_h_l_1_reg_hlint,
       stack_pointer_1_sp_int;

  LED led_1 (.in(not_1_out));
  LED led_2 (.in(not_2_out));
  not not_1 (not_1_out, nRRC_OUT);
  not not_2 (not_2_out, nRAR_OUT);
  LED led_3 (.in(ALU_M));
  LED led_4 (.in(ALU_S3));
  LED led_5 (.in(mar_v2_1_mar_int[14]));
  LED led_6 (.in(mar_v2_1_mar_int[15]));
  LED led_7 (.in(stack_pointer_1_sp_int[14]));
  LED led_8 (.in(stack_pointer_1_sp_int[15]));
  LED led_9 (.in(program_counter_1_pc_int[14]));
  LED led_10 (.in(program_counter_1_pc_int[15]));
  LED led_11 (.in(ALU_S2));
  LED led_12 (.in(ALU_S1));
  LED led_13 (.in(mar_v2_1_mar_int[12]));
  LED led_14 (.in(mar_v2_1_mar_int[13]));
  LED led_15 (.in(stack_pointer_1_sp_int[12]));
  LED led_16 (.in(stack_pointer_1_sp_int[13]));
  LED led_17 (.in(program_counter_1_pc_int[12]));
  LED led_18 (.in(program_counter_1_pc_int[13]));
  LED led_19 (.in(ALU_S0));
  LED led_20 (.in(ALU_CARRY));
  LED led_21 (.in(mar_v2_1_mar_int[10]));
  LED led_22 (.in(mar_v2_1_mar_int[11]));
  LED led_23 (.in(stack_pointer_1_sp_int[10]));
  LED led_24 (.in(stack_pointer_1_sp_int[11]));
  LED led_25 (.in(program_counter_1_pc_int[10]));
  LED led_26 (.in(program_counter_1_pc_int[11]));
  LED led_27 (.in(ALU_BIN));
  LED led_28 (.in(not_3_out));
  not not_3 (not_3_out, nALU_OUT);
  LED led_29 (.in(mar_v2_1_mar_int[8]));
  LED led_30 (.in(mar_v2_1_mar_int[9]));
  LED led_31 (.in(stack_pointer_1_sp_int[8]));
  LED led_32 (.in(stack_pointer_1_sp_int[9]));
  LED led_33 (.in(program_counter_1_pc_int[8]));
  LED led_34 (.in(program_counter_1_pc_int[9]));
  LED led_35 (.in(FR_IN));
  LED led_36 (.in(mar_v2_1_mar_int[6]));
  LED led_37 (.in(mar_v2_1_mar_int[7]));
  LED led_38 (.in(stack_pointer_1_sp_int[6]));
  LED led_39 (.in(stack_pointer_1_sp_int[7]));
  LED led_40 (.in(program_counter_1_pc_int[6]));
  LED led_41 (.in(program_counter_1_pc_int[7]));
  LED led_42 (.in(ram_eeprom_1_ram_int[7]));
  LED led_43 (.in(ram_eeprom_1_ram_int[6]));
  LED led_44 (.in(rom_1_rom_int[7]));
  LED led_45 (.in(rom_1_rom_int[6]));
  LED led_46 (.in(REG_HIN));
  LED led_47 (.in(not_4_out));
  not not_4 (not_4_out, nREG_HOUT);
  LED led_48 (.in(mar_v2_1_mar_int[4]));
  LED led_49 (.in(mar_v2_1_mar_int[5]));
  or or_1 (or_1_out, INC_MAR, INC_MAR_t);
  LED led_50 (.in(stack_pointer_1_sp_int[4]));
  LED led_51 (.in(stack_pointer_1_sp_int[5]));
  LED led_52 (.in(program_counter_1_pc_int[4]));
  LED led_53 (.in(program_counter_1_pc_int[5]));
  LED led_54 (.in(ram_eeprom_1_ram_int[5]));
  LED led_55 (.in(ram_eeprom_1_ram_int[4]));
  LED led_56 (.in(rom_1_rom_int[5]));
  LED led_57 (.in(rom_1_rom_int[4]));
  LED led_58 (.in(REG_LIN));
  LED led_59 (.in(REG_EIN));
  LED led_60 (.in(not_5_out));
  LED led_61 (.in(not_6_out));
  not not_5 (not_5_out, nREG_LOUT);
  not not_6 (not_6_out, nREG_EOUT);
  LED led_62 (.in(mar_v2_1_addr_bus[14]));
  LED led_63 (.in(mar_v2_1_addr_bus[15]));
  LED led_64 (.in(mar_v2_1_mar_int[2]));
  LED led_65 (.in(mar_v2_1_mar_int[3]));
  LED led_66 (.in(stack_pointer_1_sp_int[2]));
  LED led_67 (.in(stack_pointer_1_sp_int[3]));
  LED led_68 (.in(program_counter_1_pc_int[2]));
  LED led_69 (.in(program_counter_1_pc_int[3]));
  LED led_70 (.in(ram_eeprom_1_ram_int[3]));
  LED led_71 (.in(ram_eeprom_1_ram_int[2]));
  LED led_72 (.in(rom_1_rom_int[3]));
  LED led_73 (.in(rom_1_rom_int[2]));
  LED led_74 (.in(REG_DIN));
  LED led_75 (.in(REG_CIN));
  LED led_76 (.in(not_7_out));
  LED led_77 (.in(not_8_out));
  not not_7 (not_7_out, nREG_DOUT);
  not not_8 (not_8_out, nREG_COUT);
  LED led_78 (.in(REG_TIN));
  LED led_79 (.in(not_9_out));
  not not_9 (not_9_out, nREG_TOUT);
  LED led_80 (.in(mar_v2_1_addr_bus[12]));
  LED led_81 (.in(mar_v2_1_addr_bus[13]));
  LED led_82 (.in(mar_v2_1_mar_int[0]));
  LED led_83 (.in(mar_v2_1_mar_int[1]));
  LED led_84 (.in(stack_pointer_1_sp_int[0]));
  LED led_85 (.in(stack_pointer_1_sp_int[1]));
  Multiplexer multiplexer_1 (.sel(not_12_out), .in_0(PROG), .in_1(nPC_HLOUT), .out(multiplexer_1_out));
  LED led_86 (.in(program_counter_1_pc_int[0]));
  LED led_87 (.in(program_counter_1_pc_int[1]));
  LED led_88 (.in(ram_eeprom_1_ram_int[1]));
  LED led_89 (.in(ram_eeprom_1_ram_int[0]));
  LED led_90 (.in(rom_1_rom_int[1]));
  LED led_91 (.in(rom_1_rom_int[0]));
  LED led_92 (.in(REG_BIN));
  LED led_93 (.in(REG_AIN));
  LED led_94 (.in(not_10_out));
  LED led_95 (.in(not_11_out));
  not not_10 (not_10_out, nREG_BOUT);
  not not_11 (not_11_out, nREG_AOUT);
  LED led_96 (.in(mar_v2_1_addr_bus[10]));
  LED led_97 (.in(mar_v2_1_addr_bus[11]));
  not not_12 (not_12_out, PROG);
  LED led_98 (.in(mar_v2_1_addr_bus[8]));
  LED led_99 (.in(mar_v2_1_addr_bus[9]));
  LED led_100 (.in(not_13_out));
  LED led_101 (.in(not_14_out));
  not not_13 (not_13_out, nDEC_H);
  not not_14 (not_14_out, nINC_H);
  LED led_102 (.in(mar_v2_1_addr_bus[6]));
  LED led_103 (.in(mar_v2_1_addr_bus[7]));
  LED led_104 (.in(rom_1_bus[7]));
  LED led_105 (.in(RAM_IN));
  LED led_106 (.in(RAM_OUT));
  LED led_107 (.in(not_15_out));
  LED led_108 (.in(not_16_out));
  not not_15 (not_15_out, nPAIR_HLOUT);
  not not_16 (not_16_out, nPAIR_DEOUT);
  LED led_109 (.in(mar_v2_1_addr_bus[4]));
  LED led_110 (.in(mar_v2_1_addr_bus[5]));
  mar_v2 mar_v2_1 (
    .nMAR_OUT(nMAR_OUT), .BUS(rom_1_bus), .VCC(VCC), .GND(GND), .INC_MAR(or_1_out), .CLK(CLK_t), .nRST(nRST),
    .MAR_DATAIN(MAR_DATAIN), .PROG(PROG), .L_nH(L_nH), .MAR_LIN(MAR_LIN), .MAR_HIN(MAR_HIN),
    .ADDR_BUS(mar_v2_1_addr_bus), .MAR_INT(mar_v2_1_mar_int));
  stack_pointer stack_pointer_1 (
    .BUS(rom_1_bus), .nDEC_SP(nDEC_SP), .SP_LIN(SP_LIN), .SP_HIN(SP_HIN), .RST(RST), .VCC(VCC), .GND(GND),
    .nSP_OUT(nSP_OUT), .nINC_SP(nINC_SP), .CLK(CLK_t), .ADDR_BUS(mar_v2_1_addr_bus),
    .SP_INT(stack_pointer_1_sp_int));
  program_counter program_counter_1 (
    .nPC_HLOUT(multiplexer_1_out), .BUS(rom_1_bus), .VCC(VCC), .GND(GND), .PC_E(PC_E), .nJMP_L(nJMP_L),
    .nJMP_H(nJMP_H), .CLK(CLK_t), .nRST(nRST), .nPC_LOUT(nPC_LOUT), .nPC_HOUT(nPC_HOUT),
    .ADDR_BUS(mar_v2_1_addr_bus), .PC_INT(program_counter_1_pc_int));
  address_decoder address_decoder_1 (
    .ADDR_BUS(mar_v2_1_addr_bus), .RAM_IN(RAM_IN), .VCC(VCC), .GND(GND), .nRAM_CS(address_decoder_1_nram_cs),
    .nROM_CS(address_decoder_1_nrom_cs));  // open: nCF_CS, LCD_RS, LCD_E
  ram_eeprom ram_eeprom_1 (
    .VCC(VCC), .GND(GND), .RAM_DATAIN(RAM_DATAIN), .ADDR_BUS(mar_v2_1_addr_bus), .RAM_OUT(RAM_OUT),
    .PROG(PROG_RAM), .RAM_IN(RAM_IN), .CLK(CLK_t), .BUS(rom_1_bus), .nRAM_CS(address_decoder_1_nram_cs),
    .RAM_INT(ram_eeprom_1_ram_int));
  rom rom_1 (
    .nROM_CS(address_decoder_1_nrom_cs), .VCC(VCC), .GND(GND), .ROM_DATAIN(ROM_DATAIN), .PROG_ROM(PROG_ROM),
    .ADDR_BUS(mar_v2_1_addr_bus), .BUS(rom_1_bus), .ROM_INT(rom_1_rom_int));
  LED led_111 (.in(rom_1_bus[6]));
  LED led_112 (.in(rom_1_bus[5]));
  LED led_113 (.in(not_17_out));
  not not_17 (not_17_out, nPAIR_BCOUT);
  LED led_114 (.in(mar_v2_1_addr_bus[2]));
  LED led_115 (.in(mar_v2_1_addr_bus[3]));
  LED led_116 (.in(rom_1_bus[4]));
  LED led_117 (.in(rom_1_bus[3]));
  LED led_118 (.in(not_18_out));
  not not_18 (not_18_out, nDEC_SP);
  LED led_119 (.in(mar_v2_1_addr_bus[0]));
  LED led_120 (.in(mar_v2_1_addr_bus[1]));
  LED led_121 (.in(rom_1_bus[2]));
  LED led_122 (.in(rom_1_bus[1]));
  LED led_123 (.in(PC_E));
  LED led_124 (.in(not_19_out));
  not not_19 (not_19_out, nJMP_H);
  LED led_125 (.in(not_20_out));
  LED led_126 (.in(SP_HIN));
  not not_20 (not_20_out, nINC_SP);
  LED led_127 (.in(MAR_HIN));
  LED led_128 (.in(INC_MAR_t));
  LED led_129 (.in(rom_1_bus[7]));
  LED led_130 (.in(rom_1_bus[0]));
  instruction_decoder instruction_decoder_1 (
    .VCC(VCC), .GND(GND), .IR_BUS(IR_BUS), .STEP_0_T(STEP_0), .STEP_1_T(STEP_1), .STEP_2_T(STEP_2),
    .STEP_3_T(STEP_3), .VF(VF), .NF(NF), .CF(CF), .ZF(ZF), .nREG_AOUT(nREG_AOUT), .nREG_BOUT(nREG_BOUT),
    .nREG_COUT(nREG_COUT), .nREG_DOUT(nREG_DOUT), .nREG_EOUT(nREG_EOUT), .nREG_LOUT(nREG_LOUT),
    .nREG_HOUT(nREG_HOUT), .RAM_OUT(RAM_OUT), .nALU_OUT(nALU_OUT), .nPAIR_BCOUT(nPAIR_BCOUT),
    .nPAIR_DEOUT(nPAIR_DEOUT), .nPAIR_HLOUT(nPAIR_HLOUT), .nSP_OUT(nSP_OUT), .nPC_HLOUT(nPC_HLOUT),
    .nMAR_OUT(nMAR_OUT), .HLT(HLT_t), .nINC_H(nINC_H), .nDEC_H(nDEC_H), .nINC_SP(nINC_SP), .nDEC_SP(nDEC_SP),
    .ALU_S0(ALU_S0), .ALU_S1(ALU_S1), .ALU_S2(ALU_S2), .ALU_S3(ALU_S3), .ALU_M(ALU_M), .FR_IN(FR_IN),
    .nJMP_L(nJMP_L), .nJMP_H(nJMP_H), .PC_E(PC_E), .REG_AIN(REG_AIN), .REG_BIN(REG_BIN), .REG_CIN(REG_CIN),
    .REG_DIN(REG_DIN), .REG_EIN(REG_EIN), .REG_LIN(REG_LIN), .REG_HIN(REG_HIN), .MAR_LIN(MAR_LIN),
    .MAR_HIN(MAR_HIN), .SP_LIN(SP_LIN), .SP_HIN(SP_HIN), .IR_IN(IR_IN), .REG_OUTIN(REG_OUTIN),
    .ALU_BIN(ALU_BIN), .nREG_TMPOUT(nREG_TOUT), .REG_TMPIN(REG_TIN), .RAM_IN(RAM_IN), .nRAR_OUT(nRAR_OUT),
    .nRRC_OUT(nRRC_OUT), .ALC(ALU_CARRY), .INC_MAR(INC_MAR_t), .SC_RST(SC_RST), .nPC_HOUT(nPC_HOUT),
    .nPC_LOUT(nPC_LOUT));
  LED led_131 (.in(not_21_out));
  LED led_132 (.in(not_22_out));
  not not_21 (not_21_out, nJMP_L);
  not not_22 (not_22_out, nPC_HLOUT);
  LED led_133 (.in(not_23_out));
  LED led_134 (.in(SP_LIN));
  not not_23 (not_23_out, nSP_OUT);
  LED led_135 (.in(not_24_out));
  LED led_136 (.in(MAR_LIN));
  not not_24 (not_24_out, nMAR_OUT);
  LED led_137 (.in(rom_1_bus[6]));
  LED led_138 (.in(rom_1_bus[5]));
  LED led_139 (.in(not_25_out));
  LED led_140 (.in(not_26_out));
  not not_25 (not_25_out, nPC_LOUT);
  not not_26 (not_26_out, nPC_HOUT);
  LED led_141 (.in(rom_1_bus[4]));
  LED led_142 (.in(rom_1_bus[3]));
  and and_1 (and_1_out, CLK_t, ~PROG);  // And
  not not_27 (not_27_out, and_1_out);
  and and_2 (and_2_out, CLK_t, SC_RST);
  LED led_143 (.in(REG_OUTIN));
  LED led_144 (.in(IR_IN));
  LED led_145 (.in(rom_1_bus[2]));
  LED led_146 (.in(rom_1_bus[1]));
  LED led_147 (.in(SC_RST));
  LED led_148 (.in(HLT_t));
  LED led_149 (.in(rom_1_bus[0]));
  register_temporary register_temporary_1 (
    .VCC(VCC), .GND(GND), .REG_TIN(REG_TIN), .CLK(CLK_t), .nREG_TOUT(nREG_TOUT), .BUS(rom_1_bus),
    .REG_TINT(register_temporary_1_reg_tint));
  register_a register_a_1 (
    .VCC(VCC), .GND(GND), .REG_AIN(REG_AIN), .CLK(CLK_t), .nREG_AOUT(nREG_AOUT), .BUS(rom_1_bus));  // open: REG_AINT
  alu alu_1 (
    .BUS(rom_1_bus), .REG_AINT(undriven_2), .ALU_S3(ALU_S3), .ALU_S2(ALU_S2), .ALU_S1(ALU_S1),
    .ALU_S0(ALU_S0), .ALU_M(ALU_M), .nALU_OUT(nALU_OUT), .VCC(VCC), .GND(GND), .CLK(CLK_t),
    .ALU_BIN(ALU_BIN), .FR_IN(FR_IN), .nRRC_OUT(nRRC_OUT), .ALU_CARRY(ALU_CARRY), .nRAR_OUT(nRAR_OUT),
    .ZF(ZF), .CF(CF), .NF(NF), .VF(VF), .ALU_BUFINT(alu_1_alu_bufint), .ALU_OUTINT(alu_1_alu_outint),
    .FLAGS_INT(alu_1_flags_int));
  register_b_c register_b_c_1 (
    .REG_BIN(REG_BIN), .clk(CLK_t), .REG_CI(REG_CIN), .VCC(VCC), .GND(GND), .BUS(rom_1_bus),
    .nREG_BOUT(nREG_BOUT), .nREG_COUT(nREG_COUT), .nPAIR_BCOUT(nPAIR_BCOUT));  // open: ADDR_BUS
  // register_d_e register_d_e_1: pin names not known; wires that end beside it: REG_DIN, CLK_t, REG_EIN, VCC, GND, rom_1_bus, nREG_DOUT, nREG_EOUT, nPAIR_DEOUT, register_d_e_1_p10, mar_v2_1_addr_bus, register_d_e_1_p12, register_d_e_1_p13
  register_h_l register_h_l_1 (
    .BUS(rom_1_bus), .nDEC_H(nDEC_H), .REG_LIN(REG_LIN), .REG_HIN(REG_HIN), .RST(RST), .VCC(VCC), .GND(GND),
    .nREG_LOUT(nREG_LOUT), .nREG_HOUT(nREG_HOUT), .nPAIR_HLOUT(nPAIR_HLOUT), .nINC_H(nINC_H), .CLK(CLK_t),
    .ADDR_BUS(mar_v2_1_addr_bus), .REG_HLINT(register_h_l_1_reg_hlint));
  register_output register_output_1 (
    .CLK(CLK_t), .REG_OUTIN(REG_OUTIN), .CLK_DISP(CLK_DISP), .BUS(rom_1_bus), .VCC(VCC), .GND(GND),
    .LED_SEGOUT(register_output_1_led_segout));
  step_counter step_counter_1 (
    .nCLK(not_27_out), .VCC(VCC), .GND(GND), .SC_RST(and_2_out), .RST(RST), .STEP_0(STEP_0), .STEP_1(STEP_1),
    .STEP_2(STEP_2), .STEP_3(STEP_3), .CLR(step_counter_1_clr));
  register_instruction register_instruction_1 (
    .BUS(rom_1_bus), .CLK(CLK_t), .IR_IN(IR_IN), .VCC(VCC), .GND(GND), .IR_BUS(register_instruction_1_ir_bus));
  PowerSupply powersupply_1 (.VDD(VCC), .GND(GND));
  LED led_150 (.in(STEP_3));
  LED led_151 (.in(step_counter_1_clr));
  Multiplexer #(.Bits(8)) multiplexer_2 (
    .sel(IR_SEL), .in_0(register_instruction_1_ir_bus), .in_1(IR_DATAIN), .out(IR_BUS));
  LED led_152 (.in(register_temporary_1_reg_tint[7]));
  LED led_153 (.in(register_temporary_1_reg_tint[6]));
  LED led_154 (.in(undriven_2[7]));
  LED led_155 (.in(undriven_2[6]));
  LED led_156 (.in(alu_1_alu_bufint[7]));
  LED led_157 (.in(alu_1_alu_bufint[6]));
  LED led_158 (.in(alu_1_alu_outint[7]));
  LED led_159 (.in(alu_1_alu_outint[6]));
  LED led_160 (.in(alu_1_flags_int[0]));
  LED led_161 (.in(alu_1_flags_int[1]));
  LED led_162 (.in(undriven[7]));
  LED led_163 (.in(undriven[6]));
  LED led_164 (.in(register_d_e_1_p10[7]));
  LED led_165 (.in(register_d_e_1_p10[6]));
  LED led_166 (.in(register_d_e_1_p12[7]));
  LED led_167 (.in(register_d_e_1_p12[6]));
  LED led_168 (.in(register_d_e_1_p13[7]));
  LED led_169 (.in(register_d_e_1_p13[6]));
  LED led_170 (.in(register_h_l_1_reg_hlint[14]));
  LED led_171 (.in(register_h_l_1_reg_hlint[15]));
  LED led_172 (.in(STEP_1));
  LED led_173 (.in(STEP_2));
  LED led_174 (.in(IR_BUS[7]));
  LED led_175 (.in(IR_BUS[6]));
  and and_3 (and_3_out, AUTO_EN, CLK);
  LED led_176 (.in(register_temporary_1_reg_tint[5]));
  LED led_177 (.in(register_temporary_1_reg_tint[4]));
  LED led_178 (.in(undriven_2[5]));
  LED led_179 (.in(undriven_2[4]));
  LED led_180 (.in(alu_1_alu_bufint[5]));
  LED led_181 (.in(alu_1_alu_bufint[4]));
  LED led_182 (.in(alu_1_alu_outint[5]));
  LED led_183 (.in(alu_1_alu_outint[4]));
  LED led_184 (.in(alu_1_flags_int[2]));
  LED led_185 (.in(alu_1_flags_int[3]));
  LED led_186 (.in(undriven[5]));
  LED led_187 (.in(undriven[4]));
  LED led_188 (.in(register_d_e_1_p10[5]));
  LED led_189 (.in(register_d_e_1_p10[4]));
  LED led_190 (.in(register_d_e_1_p12[5]));
  LED led_191 (.in(register_d_e_1_p12[4]));
  LED led_192 (.in(register_d_e_1_p13[5]));
  LED led_193 (.in(register_d_e_1_p13[4]));
  LED led_194 (.in(register_h_l_1_reg_hlint[12]));
  LED led_195 (.in(register_h_l_1_reg_hlint[13]));
  LED led_196 (.in(STEP_0));
  LED led_197 (.in(IR_BUS[5]));
  LED led_198 (.in(IR_BUS[4]));
  or or_2 (or_2_out, CLK_M, and_3_out);
  LED led_199 (.in(register_temporary_1_reg_tint[3]));
  LED led_200 (.in(register_temporary_1_reg_tint[2]));
  LED led_201 (.in(undriven_2[3]));
  LED led_202 (.in(undriven_2[2]));
  LED led_203 (.in(alu_1_alu_bufint[3]));
  LED led_204 (.in(alu_1_alu_bufint[2]));
  LED led_205 (.in(alu_1_alu_outint[3]));
  LED led_206 (.in(alu_1_alu_outint[2]));
  LED led_207 (.in(undriven[3]));
  LED led_208 (.in(undriven[2]));
  LED led_209 (.in(register_d_e_1_p10[3]));
  LED led_210 (.in(register_d_e_1_p10[2]));
  LED led_211 (.in(register_d_e_1_p12[3]));
  LED led_212 (.in(register_d_e_1_p12[2]));
  LED led_213 (.in(register_d_e_1_p13[3]));
  LED led_214 (.in(register_d_e_1_p13[2]));
  LED led_215 (.in(register_h_l_1_reg_hlint[10]));
  LED led_216 (.in(register_h_l_1_reg_hlint[11]));
  LED led_217 (.in(IR_BUS[3]));
  LED led_218 (.in(IR_BUS[2]));
  and and_4 (CLK_t, ~HLT_t, ~HLT, or_2_out);  // And
  LED led_219 (.in(register_temporary_1_reg_tint[1]));
  LED led_220 (.in(register_temporary_1_reg_tint[0]));
  LED led_221 (.in(undriven_2[1]));
  LED led_222 (.in(undriven_2[0]));
  LED led_223 (.in(alu_1_alu_bufint[1]));
  LED led_224 (.in(alu_1_alu_bufint[0]));
  LED led_225 (.in(alu_1_alu_outint[1]));
  LED led_226 (.in(alu_1_alu_outint[0]));
  LED led_227 (.in(VF));
  LED led_228 (.in(NF));
  LED led_229 (.in(undriven[1]));
  LED led_230 (.in(undriven[0]));
  LED led_231 (.in(register_d_e_1_p10[1]));
  LED led_232 (.in(register_d_e_1_p10[0]));
  LED led_233 (.in(register_d_e_1_p12[1]));
  LED led_234 (.in(register_d_e_1_p12[0]));
  LED led_235 (.in(register_d_e_1_p13[1]));
  LED led_236 (.in(register_d_e_1_p13[0]));
  LED led_237 (.in(register_h_l_1_reg_hlint[8]));
  LED led_238 (.in(register_h_l_1_reg_hlint[9]));
  Seven_Seg #(.commonCathode("true"), .persistTime(13)) seven_seg_1 (
    .a(register_output_1_led_segout[1]), .b(register_output_1_led_segout[2]),
    .c(register_output_1_led_segout[3]), .d(register_output_1_led_segout[4]),
    .e(register_output_1_led_segout[5]), .f(register_output_1_led_segout[6]),
    .g(register_output_1_led_segout[7]), .dp(register_output_1_led_segout[0]),
    .common(register_output_1_led_segout[8]));
  LED led_239 (.in(IR_BUS[1]));
  LED led_240 (.in(IR_BUS[0]));
  LED led_241 (.in(CF));
  LED led_242 (.in(ZF));
  LED led_243 (.in(register_h_l_1_reg_hlint[6]));
  LED led_244 (.in(register_h_l_1_reg_hlint[7]));
  Seven_Seg #(.commonCathode("true"), .persistTime(13)) seven_seg_2 (
    .a(register_output_1_led_segout[1]), .b(register_output_1_led_segout[2]),
    .c(register_output_1_led_segout[3]), .d(register_output_1_led_segout[4]),
    .e(register_output_1_led_segout[5]), .f(register_output_1_led_segout[6]),
    .g(register_output_1_led_segout[7]), .dp(register_output_1_led_segout[0]),
    .common(register_output_1_led_segout[9]));
  LED led_245 (.in(register_h_l_1_reg_hlint[4]));
  LED led_246 (.in(register_h_l_1_reg_hlint[5]));
  LED led_247 (.in(register_h_l_1_reg_hlint[2]));
  LED led_248 (.in(register_h_l_1_reg_hlint[3]));
  Seven_Seg #(.commonCathode("true"), .persistTime(13)) seven_seg_3 (
    .a(register_output_1_led_segout[1]), .b(register_output_1_led_segout[2]),
    .c(register_output_1_led_segout[3]), .d(register_output_1_led_segout[4]),
    .e(register_output_1_led_segout[5]), .f(register_output_1_led_segout[6]),
    .g(register_output_1_led_segout[7]), .dp(register_output_1_led_segout[0]),
    .common(register_output_1_led_segout[10]));
  not not_28 (nRST, RST);
  LED led_249 (.in(register_h_l_1_reg_hlint[0]));
  LED led_250 (.in(register_h_l_1_reg_hlint[1]));
  Seven_Seg #(.commonCathode("true"), .persistTime(13)) seven_seg_4 (
    .a(register_output_1_led_segout[1]), .b(register_output_1_led_segout[2]),
    .c(register_output_1_led_segout[3]), .d(register_output_1_led_segout[4]),
    .e(register_output_1_led_segout[5]), .f(register_output_1_led_segout[6]),
    .g(register_output_1_led_segout[7]), .dp(register_output_1_led_segout[0]),
    .common(register_output_1_led_segout[11]));

  // Notes on the sheet:
  //   VCC: default 1
  //   CLK_DISP: Hz: 20
  //   CLK: Hz: 10
  //   Stack pointer
  //   Program counter
  //   MAR
  //   RAM output
  //   ROM output
  //   Control words
  //   Address bus
  //   Bus
  //   V
  //   N
  //   C
  //   Z
  //   Step
  //   Flags
  //   Register pair HL
  //   Register Temporary
  //   Register A
  //   ALU buffer
  //   ALU out
  //   Register B
  //   Register C
  //   Register D
  //   Register E
  //   Opcode
endmodule
