// Digital circuit mar.dig as structural Verilog
module mar (
  input  nMAR_OUT,
  input  MAR_LIN,
  input  MAR_HIN,
  input  CLK,
  input  VCC,
  input  GND,
  input  [7:0] BUS,
  input  [7:0] MAR_DATAIN,
  input  PROG,
  input  L_nH,
  output [15:0] ADDR_BUS,
  output [7:0] MAR_LINT,
  output [7:0] MAR_HINT
);

  wire _74245_1_pin11, _74245_1_pin12, _74245_1_pin13, _74245_1_pin14, _74245_1_pin15, _74245_1_pin16,
       _74245_1_pin17, _74245_1_pin18, _74245_2_pin19, _74245_3_pin11, _74245_3_pin12, _74245_3_pin13,
       _74245_3_pin14, _74245_3_pin15, _74245_3_pin16, _74245_3_pin17, _74245_3_pin18, _74245_4_pin11,
       _74245_4_pin12, _74245_4_pin13, _74245_4_pin14, _74245_4_pin15, _74245_4_pin16, _74245_4_pin17,
       _74245_4_pin18, and_1_out, and_2_out, and_3_out, and_4_out, bussplitter_1_d0, bussplitter_1_d1,
       bussplitter_1_d2, bussplitter_1_d3, bussplitter_1_d4, bussplitter_1_d5, bussplitter_1_d6,
       bussplitter_1_d7, not_2_out, or_1_out, or_2_out;

  BusSplitter #(.Bits(8)) bussplitter_1 (
    .D(BUS), .OE(VCC), .D0(bussplitter_1_d0), .D1(bussplitter_1_d1), .D2(bussplitter_1_d2),
    .D3(bussplitter_1_d3), .D4(bussplitter_1_d4), .D5(bussplitter_1_d5), .D6(bussplitter_1_d6),
    .D7(bussplitter_1_d7));
  _74245 _74245_1 (
    .pin1(VCC), .pin2(bussplitter_1_d0), .pin3(bussplitter_1_d1), .pin4(bussplitter_1_d2),
    .pin5(bussplitter_1_d3), .pin6(bussplitter_1_d4), .pin7(bussplitter_1_d5), .pin8(bussplitter_1_d6),
    .pin9(bussplitter_1_d7), .pin10(GND), .pin11(_74245_1_pin11), .pin12(_74245_1_pin12),
    .pin13(_74245_1_pin13), .pin14(_74245_1_pin14), .pin15(_74245_1_pin15), .pin16(_74245_1_pin16),
    .pin17(_74245_1_pin17), .pin18(_74245_1_pin18), .pin19(PROG), .pin20(VCC));
  _74245 _74245_2 (
    .pin1(VCC), .pin2(MAR_DATAIN[0]), .pin3(MAR_DATAIN[1]), .pin4(MAR_DATAIN[2]), .pin5(MAR_DATAIN[3]),
    .pin6(MAR_DATAIN[4]), .pin7(MAR_DATAIN[5]), .pin8(MAR_DATAIN[6]), .pin9(MAR_DATAIN[7]), .pin10(GND),
    .pin11(_74245_1_pin11), .pin12(_74245_1_pin12), .pin13(_74245_1_pin13), .pin14(_74245_1_pin14),
    .pin15(_74245_1_pin15), .pin16(_74245_1_pin16), .pin17(_74245_1_pin17), .pin18(_74245_1_pin18),
    .pin19(_74245_2_pin19), .pin20(VCC));
  not not_1 (_74245_2_pin19, PROG);
  not not_2 (not_2_out, L_nH);
  and and_1 (and_1_out, MAR_LIN, CLK);
  and and_2 (and_2_out, PROG, L_nH);
  and and_3 (and_3_out, CLK, MAR_HIN);
  and and_4 (and_4_out, PROG, not_2_out);
  or or_1 (or_1_out, and_1_out, and_2_out);
  or or_2 (or_2_out, and_3_out, and_4_out);
  PowerSupply powersupply_1 (.VDD(VCC), .GND(GND));
  _74573 _74573_1 (
    .pin1(GND), .pin2(_74245_1_pin18), .pin3(_74245_1_pin17), .pin4(_74245_1_pin16), .pin5(_74245_1_pin15),
    .pin6(_74245_1_pin14), .pin7(_74245_1_pin13), .pin8(_74245_1_pin12), .pin9(_74245_1_pin11), .pin10(GND),
    .pin11(or_1_out), .pin12(MAR_LINT[7]), .pin13(MAR_LINT[6]), .pin14(MAR_LINT[5]), .pin15(MAR_LINT[4]),
    .pin16(MAR_LINT[3]), .pin17(MAR_LINT[2]), .pin18(MAR_LINT[1]), .pin19(MAR_LINT[0]), .pin20(VCC));
  _74573 _74573_2 (
    .pin1(GND), .pin2(_74245_1_pin18), .pin3(_74245_1_pin17), .pin4(_74245_1_pin16), .pin5(_74245_1_pin15),
    .pin6(_74245_1_pin14), .pin7(_74245_1_pin13), .pin8(_74245_1_pin12), .pin9(_74245_1_pin11), .pin10(GND),
    .pin11(or_2_out), .pin12(MAR_HINT[7]), .pin13(MAR_HINT[6]), .pin14(MAR_HINT[5]), .pin15(MAR_HINT[4]),
    .pin16(MAR_HINT[3]), .pin17(MAR_HINT[2]), .pin18(MAR_HINT[1]), .pin19(MAR_HINT[0]), .pin20(VCC));
  LED led_1 (.in(MAR_LINT[0]));
  LED led_2 (.in(MAR_LINT[1]));
  LED led_3 (.in(MAR_LINT[2]));
  LED led_4 (.in(MAR_LINT[3]));
  LED led_5 (.in(MAR_LINT[4]));
  LED led_6 (.in(MAR_LINT[5]));
  LED led_7 (.in(MAR_LINT[6]));
  LED led_8 (.in(MAR_LINT[7]));
  LED led_9 (.in(MAR_HINT[0]));
  LED led_10 (.in(MAR_HINT[1]));
  LED led_11 (.in(MAR_HINT[2]));
  LED led_12 (.in(MAR_HINT[3]));
  LED led_13 (.in(MAR_HINT[4]));
  LED led_14 (.in(MAR_HINT[5]));
  LED led_15 (.in(MAR_HINT[6]));
  LED led_16 (.in(MAR_HINT[7]));
  _74245 _74245_3 (
    .pin1(VCC), .pin2(MAR_LINT[0]), .pin3(MAR_LINT[1]), .pin4(MAR_LINT[2]), .pin5(MAR_LINT[3]),
    .pin6(MAR_LINT[4]), .pin7(MAR_LINT[5]), .pin8(MAR_LINT[6]), .pin9(MAR_LINT[7]), .pin10(GND),
    .pin11(_74245_3_pin11), .pin12(_74245_3_pin12), .pin13(_74245_3_pin13), .pin14(_74245_3_pin14),
    .pin15(_74245_3_pin15), .pin16(_74245_3_pin16), .pin17(_74245_3_pin17), .pin18(_74245_3_pin18),
    .pin19(nMAR_OUT), .pin20(VCC));
  _74245 _74245_4 (
    .pin1(VCC), .pin2(MAR_HINT[0]), .pin3(MAR_HINT[1]), .pin4(MAR_HINT[2]), .pin5(MAR_HINT[3]),
    .pin6(MAR_HINT[4]), .pin7(MAR_HINT[5]), .pin8(MAR_HINT[6]), .pin9(MAR_HINT[7]), .pin10(GND),
    .pin11(_74245_4_pin11), .pin12(_74245_4_pin12), .pin13(_74245_4_pin13), .pin14(_74245_4_pin14),
    .pin15(_74245_4_pin15), .pin16(_74245_4_pin16), .pin17(_74245_4_pin17), .pin18(_74245_4_pin18),
    .pin19(nMAR_OUT), .pin20(VCC));
  BusSplitter #(.Bits(16)) bussplitter_2 (
    .D(ADDR_BUS), .OE(GND), .D0(_74245_3_pin18), .D1(_74245_3_pin17), .D2(_74245_3_pin16),
    .D3(_74245_3_pin15), .D4(_74245_3_pin14), .D5(_74245_3_pin13), .D6(_74245_3_pin12), .D7(_74245_3_pin11),
    .D8(_74245_4_pin18), .D9(_74245_4_pin17), .D10(_74245_4_pin16), .D11(_74245_4_pin15),
    .D12(_74245_4_pin14), .D13(_74245_4_pin13), .D14(_74245_4_pin12), .D15(_74245_4_pin11));

  // Notes on the sheet:
  //   nMAR_OUT: default 1
  //   VCC: default 1
  //   Actual DIP switches
endmodule
