// Digital circuit mar_v2.dig as structural Verilog
module mar_v2 (
  input  nMAR_OUT,
  input  [7:0] BUS,
  input  VCC,
  input  GND,
  input  INC_MAR,
  input  CLK,
  input  nRST,
  input  [7:0] MAR_DATAIN,
  input  PROG,
  input  L_nH,
  input  MAR_LIN,
  input  MAR_HIN,
  output [15:0] ADDR_BUS,
  output [15:0] MAR_INT
);

  wire _74161_1_pin9, _74161_1_pin15, _74161_2_pin15, _74161_3_pin9, _74161_3_pin15, _74245_1_pin11,
       _74245_1_pin12, _74245_1_pin13, _74245_1_pin14, _74245_1_pin15, _74245_1_pin16, _74245_1_pin17,
       _74245_1_pin18, _74245_2_pin19, _74245_3_pin11, _74245_3_pin12, _74245_3_pin13, _74245_3_pin14,
       _74245_3_pin15, _74245_3_pin16, _74245_3_pin17, _74245_3_pin18, _74245_4_pin11, _74245_4_pin12,
       _74245_4_pin13, _74245_4_pin14, _74245_4_pin15, _74245_4_pin16, _74245_4_pin17, _74245_4_pin18,
       and_1_out, and_2_out, and_3_out, bussplitter_1_d0, bussplitter_1_d1, bussplitter_1_d2,
       bussplitter_1_d3, bussplitter_1_d4, bussplitter_1_d5, bussplitter_1_d6, bussplitter_1_d7, not_2_out,
       not_5_out, or_1_out, or_2_out;

  BusSplitter #(.Bits(8)) bussplitter_1 (
    .D(BUS), .OE(VCC), .D0(bussplitter_1_d0), .D1(bussplitter_1_d1), .D2(bussplitter_1_d2),
    .D3(bussplitter_1_d3), .D4(bussplitter_1_d4), .D5(bussplitter_1_d5), .D6(bussplitter_1_d6),
    .D7(bussplitter_1_d7));
  _74245 _74245_1 (
    .pin1(VCC), .pin2(bussplitter_1_d0), .pin3(bussplitter_1_d1), .pin4(bussplitter_1_d2),
    .pin5(bussplitter_1_d3), .pin6(bussplitter_1_d4), .pin7(bussplitter_1_d5), .pin8(bussplitter_1_d6),
    .pin9(bussplitter_1_d7), .pin10(GND), .pin11(_74245_1_pin11), .pin12(_74245_1_pin12),
    .pin13(_74245_1_pin13), .pin14(_74245_1_pin14), .pin15(_74245_1_pin15), .pin16(_74245_1_pin16),
    .pin17(_74245_1_pin17), .pin18(_74245_1_pin18), .pin19(PROG), .pin20(VCC));
  _74245 _74245_2 (
    .pin1(VCC), .pin2(MAR_DATAIN[0]), .pin3(MAR_DATAIN[1]), .pin4(MAR_DATAIN[2]), .pin5(MAR_DATAIN[3]),
    .pin6(MAR_DATAIN[4]), .pin7(MAR_DATAIN[5]), .pin8(MAR_DATAIN[6]), .pin9(MAR_DATAIN[7]), .pin10(GND),
    .pin11(_74245_1_pin11), .pin12(_74245_1_pin12), .pin13(_74245_1_pin13), .pin14(_74245_1_pin14),
    .pin15(_74245_1_pin15), .pin16(_74245_1_pin16), .pin17(_74245_1_pin17), .pin18(_74245_1_pin18),
    .pin19(_74245_2_pin19), .pin20(VCC));
  not not_1 (_74245_2_pin19, PROG);
  not not_2 (not_2_out, L_nH);
  and and_1 (and_1_out, L_nH, PROG);
  and and_2 (and_2_out, PROG, not_2_out);
  or or_1 (or_1_out, MAR_LIN, and_1_out);
  or or_2 (or_2_out, MAR_HIN, and_2_out);
  PowerSupply powersupply_1 (.VDD(VCC), .GND(GND));
  _74161 _74161_1 (
    .pin1(nRST), .pin2(CLK), .pin3(_74245_1_pin18), .pin4(_74245_1_pin17), .pin5(_74245_1_pin16),
    .pin6(_74245_1_pin15), .pin7(INC_MAR), .pin8(GND), .pin9(_74161_1_pin9), .pin10(VCC), .pin11(MAR_INT[3]),
    .pin12(MAR_INT[2]), .pin13(MAR_INT[1]), .pin14(MAR_INT[0]), .pin15(_74161_1_pin15), .pin16(VCC));
  not not_3 (_74161_1_pin9, or_1_out);
  _74161 _74161_2 (
    .pin1(nRST), .pin2(CLK), .pin3(_74245_1_pin14), .pin4(_74245_1_pin13), .pin5(_74245_1_pin12),
    .pin6(_74245_1_pin11), .pin7(INC_MAR), .pin8(GND), .pin9(_74161_1_pin9), .pin10(_74161_1_pin15),
    .pin11(MAR_INT[7]), .pin12(MAR_INT[6]), .pin13(MAR_INT[5]), .pin14(MAR_INT[4]), .pin15(_74161_2_pin15),
    .pin16(VCC));
  _74161 _74161_3 (
    .pin1(nRST), .pin2(CLK), .pin3(_74245_1_pin18), .pin4(_74245_1_pin17), .pin5(_74245_1_pin16),
    .pin6(_74245_1_pin15), .pin7(INC_MAR), .pin8(GND), .pin9(_74161_3_pin9), .pin10(_74161_2_pin15),
    .pin11(MAR_INT[11]), .pin12(MAR_INT[10]), .pin13(MAR_INT[9]), .pin14(MAR_INT[8]), .pin15(_74161_3_pin15),
    .pin16(VCC));
  not not_4 (_74161_3_pin9, or_2_out);
  _74161 _74161_4 (
    .pin1(nRST), .pin2(CLK), .pin3(_74245_1_pin14), .pin4(_74245_1_pin13), .pin5(_74245_1_pin12),
    .pin6(_74245_1_pin11), .pin7(INC_MAR), .pin8(GND), .pin9(_74161_3_pin9), .pin10(_74161_3_pin15),
    .pin11(MAR_INT[15]), .pin12(MAR_INT[14]), .pin13(MAR_INT[13]), .pin14(MAR_INT[12]), .pin16(VCC));  // open: pin15
  LED led_1 (.in(MAR_INT[15]));
  LED led_2 (.in(MAR_INT[14]));
  LED led_3 (.in(MAR_INT[13]));
  LED led_4 (.in(MAR_INT[12]));
  LED led_5 (.in(MAR_INT[11]));
  LED led_6 (.in(MAR_INT[10]));
  LED led_7 (.in(MAR_INT[9]));
  LED led_8 (.in(MAR_INT[8]));
  LED led_9 (.in(MAR_INT[7]));
  LED led_10 (.in(MAR_INT[6]));
  LED led_11 (.in(MAR_INT[5]));
  LED led_12 (.in(MAR_INT[4]));
  LED led_13 (.in(MAR_INT[3]));
  LED led_14 (.in(MAR_INT[2]));
  LED led_15 (.in(MAR_INT[1]));
  LED led_16 (.in(MAR_INT[0]));
  not not_5 (not_5_out, PROG);
  and and_3 (and_3_out, not_5_out, nMAR_OUT);
  _74245 _74245_3 (
    .pin1(VCC), .pin2(MAR_INT[0]), .pin3(MAR_INT[1]), .pin4(MAR_INT[2]), .pin5(MAR_INT[3]),
    .pin6(MAR_INT[4]), .pin7(MAR_INT[5]), .pin8(MAR_INT[6]), .pin9(MAR_INT[7]), .pin10(GND),
    .pin11(_74245_3_pin11), .pin12(_74245_3_pin12), .pin13(_74245_3_pin13), .pin14(_74245_3_pin14),
    .pin15(_74245_3_pin15), .pin16(_74245_3_pin16), .pin17(_74245_3_pin17), .pin18(_74245_3_pin18),
    .pin19(and_3_out), .pin20(VCC));
  _74245 _74245_4 (
    .pin1(VCC), .pin2(MAR_INT[8]), .pin3(MAR_INT[9]), .pin4(MAR_INT[10]), .pin5(MAR_INT[11]),
    .pin6(MAR_INT[12]), .pin7(MAR_INT[13]), .pin8(MAR_INT[14]), .pin9(MAR_INT[15]), .pin10(GND),
    .pin11(_74245_4_pin11), .pin12(_74245_4_pin12), .pin13(_74245_4_pin13), .pin14(_74245_4_pin14),
    .pin15(_74245_4_pin15), .pin16(_74245_4_pin16), .pin17(_74245_4_pin17), .pin18(_74245_4_pin18),
    .pin19(and_3_out), .pin20(VCC));
  BusSplitter #(.Bits(16)) bussplitter_2 (
    .D(ADDR_BUS), .OE(GND), .D0(_74245_3_pin18), .D1(_74245_3_pin17), .D2(_74245_3_pin16),
    .D3(_74245_3_pin15), .D4(_74245_3_pin14), .D5(_74245_3_pin13), .D6(_74245_3_pin12), .D7(_74245_3_pin11),
    .D8(_74245_4_pin18), .D9(_74245_4_pin17), .D10(_74245_4_pin16), .D11(_74245_4_pin15),
    .D12(_74245_4_pin14), .D13(_74245_4_pin13), .D14(_74245_4_pin12), .D15(_74245_4_pin11));

  // Notes on the sheet:
  //   nMAR_OUT: default 1
  //   VCC: default 1
  //   nRST: default 1
  //   Actual DIP switches
endmodule
