// Digital circuit program_counter.dig as structural Verilog
module program_counter (
  input  nPC_HLOUT,
  input  [7:0] BUS,
  input  VCC,
  input  GND,
  input  PC_E,
  input  nJMP_L,
  input  nJMP_H,
  input  CLK,
  input  nRST,
  input  nPC_LOUT,
  input  nPC_HOUT,
  output [15:0] ADDR_BUS,
  output [15:0] PC_INT
);

  wire _74161_1_pin15, _74161_2_pin15, _74161_3_pin15, _74245_3_pin11, _74245_3_pin12, _74245_3_pin13,
       _74245_3_pin14, _74245_3_pin15, _74245_3_pin16, _74245_3_pin17, _74245_3_pin18, _74245_4_pin11,
       _74245_4_pin12, _74245_4_pin13, _74245_4_pin14, _74245_4_pin15, _74245_4_pin16, _74245_4_pin17,
       _74245_4_pin18, and_1_out, bussplitter_1_d0, bussplitter_1_d1, bussplitter_1_d2, bussplitter_1_d3,
       bussplitter_1_d4, bussplitter_1_d5, bussplitter_1_d6, bussplitter_1_d7;

  and and_1 (and_1_out, nPC_HOUT, nPC_LOUT);
  BusSplitter #(.Bits(8)) bussplitter_1 (
    .D(BUS), .OE(and_1_out), .D0(bussplitter_1_d0), .D1(bussplitter_1_d1), .D2(bussplitter_1_d2),
    .D3(bussplitter_1_d3), .D4(bussplitter_1_d4), .D5(bussplitter_1_d5), .D6(bussplitter_1_d6),
    .D7(bussplitter_1_d7));
  PowerSupply powersupply_1 (.VDD(VCC), .GND(GND));
  _74161 _74161_1 (
    .pin1(nRST), .pin2(CLK), .pin3(bussplitter_1_d0), .pin4(bussplitter_1_d1), .pin5(bussplitter_1_d2),
    .pin6(bussplitter_1_d3), .pin7(PC_E), .pin8(GND), .pin9(nJMP_L), .pin10(VCC), .pin11(PC_INT[3]),
    .pin12(PC_INT[2]), .pin13(PC_INT[1]), .pin14(PC_INT[0]), .pin15(_74161_1_pin15), .pin16(VCC));
  _74161 _74161_2 (
    .pin1(nRST), .pin2(CLK), .pin3(bussplitter_1_d4), .pin4(bussplitter_1_d5), .pin5(bussplitter_1_d6),
    .pin6(bussplitter_1_d7), .pin7(PC_E), .pin8(GND), .pin9(nJMP_L), .pin10(_74161_1_pin15),
    .pin11(PC_INT[7]), .pin12(PC_INT[6]), .pin13(PC_INT[5]), .pin14(PC_INT[4]), .pin15(_74161_2_pin15),
    .pin16(VCC));
  _74161 _74161_3 (
    .pin1(nRST), .pin2(CLK), .pin3(bussplitter_1_d0), .pin4(bussplitter_1_d1), .pin5(bussplitter_1_d2),
    .pin6(bussplitter_1_d3), .pin7(PC_E), .pin8(GND), .pin9(nJMP_H), .pin10(_74161_2_pin15),
    .pin11(PC_INT[11]), .pin12(PC_INT[10]), .pin13(PC_INT[9]), .pin14(PC_INT[8]), .pin15(_74161_3_pin15),
    .pin16(VCC));
  _74161 _74161_4 (
    .pin1(nRST), .pin2(CLK), .pin3(bussplitter_1_d4), .pin4(bussplitter_1_d5), .pin5(bussplitter_1_d6),
    .pin6(bussplitter_1_d7), .pin7(PC_E), .pin8(GND), .pin9(nJMP_H), .pin10(_74161_3_pin15),
    .pin11(PC_INT[15]), .pin12(PC_INT[14]), .pin13(PC_INT[13]), .pin14(PC_INT[12]), .pin16(VCC));  // open: pin15
  LED led_1 (.in(PC_INT[15]));
  LED led_2 (.in(PC_INT[14]));
  LED led_3 (.in(PC_INT[13]));
  LED led_4 (.in(PC_INT[12]));
  LED led_5 (.in(PC_INT[11]));
  LED led_6 (.in(PC_INT[10]));
  LED led_7 (.in(PC_INT[9]));
  LED led_8 (.in(PC_INT[8]));
  LED led_9 (.in(PC_INT[7]));
  LED led_10 (.in(PC_INT[6]));
  LED led_11 (.in(PC_INT[5]));
  LED led_12 (.in(PC_INT[4]));
  LED led_13 (.in(PC_INT[3]));
  LED led_14 (.in(PC_INT[2]));
  LED led_15 (.in(PC_INT[1]));
  LED led_16 (.in(PC_INT[0]));
  _74245 _74245_1 (
    .pin1(VCC), .pin2(PC_INT[0]), .pin3(PC_INT[1]), .pin4(PC_INT[2]), .pin5(PC_INT[3]), .pin6(PC_INT[4]),
    .pin7(PC_INT[5]), .pin8(PC_INT[6]), .pin9(PC_INT[7]), .pin10(GND), .pin11(bussplitter_1_d7),
    .pin12(bussplitter_1_d6), .pin13(bussplitter_1_d5), .pin14(bussplitter_1_d4), .pin15(bussplitter_1_d3),
    .pin16(bussplitter_1_d2), .pin17(bussplitter_1_d1), .pin18(bussplitter_1_d0), .pin19(nPC_LOUT),
    .pin20(VCC));
  _74245 _74245_2 (
    .pin1(VCC), .pin2(PC_INT[8]), .pin3(PC_INT[9]), .pin4(PC_INT[10]), .pin5(PC_INT[11]), .pin6(PC_INT[12]),
    .pin7(PC_INT[13]), .pin8(PC_INT[14]), .pin9(PC_INT[15]), .pin10(GND), .pin11(bussplitter_1_d7),
    .pin12(bussplitter_1_d6), .pin13(bussplitter_1_d5), .pin14(bussplitter_1_d4), .pin15(bussplitter_1_d3),
    .pin16(bussplitter_1_d2), .pin17(bussplitter_1_d1), .pin18(bussplitter_1_d0), .pin19(nPC_HOUT),
    .pin20(VCC));
  _74245 _74245_3 (
    .pin1(VCC), .pin2(PC_INT[0]), .pin3(PC_INT[1]), .pin4(PC_INT[2]), .pin5(PC_INT[3]), .pin6(PC_INT[4]),
    .pin7(PC_INT[5]), .pin8(PC_INT[6]), .pin9(PC_INT[7]), .pin10(GND), .pin11(_74245_3_pin11),
    .pin12(_74245_3_pin12), .pin13(_74245_3_pin13), .pin14(_74245_3_pin14), .pin15(_74245_3_pin15),
    .pin16(_74245_3_pin16), .pin17(_74245_3_pin17), .pin18(_74245_3_pin18), .pin19(nPC_HLOUT), .pin20(VCC));
  _74245 _74245_4 (
    .pin1(VCC), .pin2(PC_INT[8]), .pin3(PC_INT[9]), .pin4(PC_INT[10]), .pin5(PC_INT[11]), .pin6(PC_INT[12]),
    .pin7(PC_INT[13]), .pin8(PC_INT[14]), .pin9(PC_INT[15]), .pin10(GND), .pin11(_74245_4_pin11),
    .pin12(_74245_4_pin12), .pin13(_74245_4_pin13), .pin14(_74245_4_pin14), .pin15(_74245_4_pin15),
    .pin16(_74245_4_pin16), .pin17(_74245_4_pin17), .pin18(_74245_4_pin18), .pin19(nPC_HLOUT), .pin20(VCC));
  BusSplitter #(.Bits(16)) bussplitter_2 (
    .D(ADDR_BUS), .OE(GND), .D0(_74245_3_pin18), .D1(_74245_3_pin17), .D2(_74245_3_pin16),
    .D3(_74245_3_pin15), .D4(_74245_3_pin14), .D5(_74245_3_pin13), .D6(_74245_3_pin12), .D7(_74245_3_pin11),
    .D8(_74245_4_pin18), .D9(_74245_4_pin17), .D10(_74245_4_pin16), .D11(_74245_4_pin15),
    .D12(_74245_4_pin14), .D13(_74245_4_pin13), .D14(_74245_4_pin12), .D15(_74245_4_pin11));

  // Notes on the sheet:
  //   nPC_HLOUT: default 1
  //   VCC: default 1
  //   nJMP_L: default 1
  //   nJMP_H: default 1
  //   nRST: default 1
  //   nPC_LOUT: default 1
  //   nPC_HOUT: default 1
endmodule
