// Digital circuit ram_eeprom.dig as structural Verilog
module ram_eeprom (
  input  VCC,
  input  GND,
  input  [7:0] RAM_DATAIN,
  input  [15:0] ADDR_BUS,
  input  RAM_OUT,
  input  PROG,
  input  RAM_IN,
  input  CLK,
  input  [7:0] BUS,
  input  nRAM_CS,
  output [7:0] RAM_INT
);

  wire _74245_2_pin1, _74245_2_pin11, _74245_2_pin12, _74245_2_pin13, _74245_2_pin14, _74245_2_pin15,
       _74245_2_pin16, _74245_2_pin17, _74245_2_pin18, _74245_2_pin19, and_1_out, nor_1_out, nor_2_out,
       not_1_out;
  wire [7:0] eeprom_1_d;

  nor nor_1 (nor_1_out, nRAM_CS, ~nor_2_out, GND);  // NOr
  EEPROM #(.AddrBits(15), .Bits(8)) eeprom_1 (
    .A(ADDR_BUS[14:0]), .CS(~nRAM_CS), .WE(~nor_2_out), .OE(~GND), .D(eeprom_1_d));
  BusSplitter #(.Bits(8)) bussplitter_1 (
    .D(eeprom_1_d), .OE(nor_1_out), .D0(RAM_INT[0]), .D1(RAM_INT[1]), .D2(RAM_INT[2]), .D3(RAM_INT[3]),
    .D4(RAM_INT[4]), .D5(RAM_INT[5]), .D6(RAM_INT[6]), .D7(RAM_INT[7]));
  and and_1 (and_1_out, RAM_IN, CLK);
  not not_1 (not_1_out, PROG);
  nor nor_2 (nor_2_out, PROG, and_1_out);
  PowerSupply powersupply_1 (.VDD(VCC), .GND(GND));
  _74245 _74245_1 (
    .pin1(GND), .pin2(RAM_INT[0]), .pin3(RAM_INT[1]), .pin4(RAM_INT[2]), .pin5(RAM_INT[3]),
    .pin6(RAM_INT[4]), .pin7(RAM_INT[5]), .pin8(RAM_INT[6]), .pin9(RAM_INT[7]), .pin10(GND),
    .pin11(RAM_DATAIN[7]), .pin12(RAM_DATAIN[6]), .pin13(RAM_DATAIN[5]), .pin14(RAM_DATAIN[4]),
    .pin15(RAM_DATAIN[3]), .pin16(RAM_DATAIN[2]), .pin17(RAM_DATAIN[1]), .pin18(RAM_DATAIN[0]),
    .pin19(not_1_out), .pin20(VCC));
  _74245 _74245_2 (
    .pin1(_74245_2_pin1), .pin2(RAM_INT[0]), .pin3(RAM_INT[1]), .pin4(RAM_INT[2]), .pin5(RAM_INT[3]),
    .pin6(RAM_INT[4]), .pin7(RAM_INT[5]), .pin8(RAM_INT[6]), .pin9(RAM_INT[7]), .pin10(GND),
    .pin11(_74245_2_pin11), .pin12(_74245_2_pin12), .pin13(_74245_2_pin13), .pin14(_74245_2_pin14),
    .pin15(_74245_2_pin15), .pin16(_74245_2_pin16), .pin17(_74245_2_pin17), .pin18(_74245_2_pin18),
    .pin19(_74245_2_pin19), .pin20(VCC));
  not not_2 (_74245_2_pin1, and_1_out);
  BusSplitter #(.Bits(8)) bussplitter_2 (
    .D(BUS), .OE(and_1_out), .D0(_74245_2_pin18), .D1(_74245_2_pin17), .D2(_74245_2_pin16),
    .D3(_74245_2_pin15), .D4(_74245_2_pin14), .D5(_74245_2_pin13), .D6(_74245_2_pin12), .D7(_74245_2_pin11));
  nor nor_3 (_74245_2_pin19, and_1_out, RAM_OUT);

  // Notes on the sheet:
  //   VCC: default 1
  //   62256
  //   contents of eeprom_1 (hex, n*v repeats v):
  //   3e,3,32,ff,0,3e,5,32,fe,0,3e,f,32,fd,0,3a,ff,0,21,fe,0,86,32,ff
  //   ,0,6d,86,32,fe,0,6d,c3,f
  //   Actual DIP switches
endmodule
