// Digital circuit register_b_c.dig as structural Verilog
module register_b_c (
  input  REG_BIN,
  input  clk,
  input  REG_CI,
  input  VCC,
  input  GND,
  input  [7:0] BUS,
  input  nREG_BOUT,
  input  nREG_COUT,
  input  nPAIR_BCOUT,
  output [15:0] ADDR_BUS
);

  wire _74245_3_pin11, _74245_3_pin12, _74245_3_pin13, _74245_3_pin14, _74245_3_pin15, _74245_3_pin16,
       _74245_3_pin17, _74245_3_pin18, _74245_4_pin11, _74245_4_pin12, _74245_4_pin13, _74245_4_pin14,
       _74245_4_pin15, _74245_4_pin16, _74245_4_pin17, _74245_4_pin18, _74573_1_pin11, _74573_1_pin12,
       _74573_1_pin13, _74573_1_pin14, _74573_1_pin15, _74573_1_pin16, _74573_1_pin17, _74573_1_pin18,
       _74573_1_pin19, _74573_2_pin11, _74573_2_pin12, _74573_2_pin13, _74573_2_pin14, _74573_2_pin15,
       _74573_2_pin16, _74573_2_pin17, _74573_2_pin18, _74573_2_pin19, and_1_out, bussplitter_1_d0,
       bussplitter_1_d1, bussplitter_1_d2, bussplitter_1_d3, bussplitter_1_d4, bussplitter_1_d5,
       bussplitter_1_d6, bussplitter_1_d7;

  and and_1 (and_1_out, nREG_BOUT, nREG_COUT);
  BusSplitter #(.Bits(8)) bussplitter_1 (
    .D(BUS), .OE(and_1_out), .D0(bussplitter_1_d0), .D1(bussplitter_1_d1), .D2(bussplitter_1_d2),
    .D3(bussplitter_1_d3), .D4(bussplitter_1_d4), .D5(bussplitter_1_d5), .D6(bussplitter_1_d6),
    .D7(bussplitter_1_d7));
  PowerSupply powersupply_1 (.VDD(VCC), .GND(GND));
  _74573 _74573_1 (
    .pin1(GND), .pin2(bussplitter_1_d0), .pin3(bussplitter_1_d1), .pin4(bussplitter_1_d2),
    .pin5(bussplitter_1_d3), .pin6(bussplitter_1_d4), .pin7(bussplitter_1_d5), .pin8(bussplitter_1_d6),
    .pin9(bussplitter_1_d7), .pin10(GND), .pin11(_74573_1_pin11), .pin12(_74573_1_pin12),
    .pin13(_74573_1_pin13), .pin14(_74573_1_pin14), .pin15(_74573_1_pin15), .pin16(_74573_1_pin16),
    .pin17(_74573_1_pin17), .pin18(_74573_1_pin18), .pin19(_74573_1_pin19), .pin20(VCC));
  and and_2 (_74573_1_pin11, REG_BIN, clk);
  _74573 _74573_2 (
    .pin1(GND), .pin2(bussplitter_1_d0), .pin3(bussplitter_1_d1), .pin4(bussplitter_1_d2),
    .pin5(bussplitter_1_d3), .pin6(bussplitter_1_d4), .pin7(bussplitter_1_d5), .pin8(bussplitter_1_d6),
    .pin9(bussplitter_1_d7), .pin10(GND), .pin11(_74573_2_pin11), .pin12(_74573_2_pin12),
    .pin13(_74573_2_pin13), .pin14(_74573_2_pin14), .pin15(_74573_2_pin15), .pin16(_74573_2_pin16),
    .pin17(_74573_2_pin17), .pin18(_74573_2_pin18), .pin19(_74573_2_pin19), .pin20(VCC));
  and and_3 (_74573_2_pin11, REG_CI, clk);
  LED led_1 (.in(_74573_1_pin19));
  LED led_2 (.in(_74573_1_pin18));
  LED led_3 (.in(_74573_1_pin17));
  LED led_4 (.in(_74573_1_pin16));
  LED led_5 (.in(_74573_1_pin15));
  LED led_6 (.in(_74573_1_pin14));
  LED led_7 (.in(_74573_1_pin13));
  LED led_8 (.in(_74573_1_pin12));
  LED led_9 (.in(_74573_2_pin19));
  LED led_10 (.in(_74573_2_pin18));
  LED led_11 (.in(_74573_2_pin17));
  LED led_12 (.in(_74573_2_pin16));
  LED led_13 (.in(_74573_2_pin15));
  LED led_14 (.in(_74573_2_pin14));
  LED led_15 (.in(_74573_2_pin13));
  LED led_16 (.in(_74573_2_pin12));
  _74245 _74245_1 (
    .pin1(VCC), .pin2(_74573_1_pin19), .pin3(_74573_1_pin18), .pin4(_74573_1_pin17), .pin5(_74573_1_pin16),
    .pin6(_74573_1_pin15), .pin7(_74573_1_pin14), .pin8(_74573_1_pin13), .pin9(_74573_1_pin12), .pin10(GND),
    .pin11(bussplitter_1_d7), .pin12(bussplitter_1_d6), .pin13(bussplitter_1_d5), .pin14(bussplitter_1_d4),
    .pin15(bussplitter_1_d3), .pin16(bussplitter_1_d2), .pin17(bussplitter_1_d1), .pin18(bussplitter_1_d0),
    .pin19(nREG_BOUT), .pin20(VCC));
  _74245 _74245_2 (
    .pin1(VCC), .pin2(_74573_2_pin19), .pin3(_74573_2_pin18), .pin4(_74573_2_pin17), .pin5(_74573_2_pin16),
    .pin6(_74573_2_pin15), .pin7(_74573_2_pin14), .pin8(_74573_2_pin13), .pin9(_74573_2_pin12), .pin10(GND),
    .pin11(bussplitter_1_d7), .pin12(bussplitter_1_d6), .pin13(bussplitter_1_d5), .pin14(bussplitter_1_d4),
    .pin15(bussplitter_1_d3), .pin16(bussplitter_1_d2), .pin17(bussplitter_1_d1), .pin18(bussplitter_1_d0),
    .pin19(nREG_COUT), .pin20(VCC));
  _74245 _74245_3 (
    .pin1(VCC), .pin2(_74573_1_pin19), .pin3(_74573_1_pin18), .pin4(_74573_1_pin17), .pin5(_74573_1_pin16),
    .pin6(_74573_1_pin15), .pin7(_74573_1_pin14), .pin8(_74573_1_pin13), .pin9(_74573_1_pin12), .pin10(GND),
    .pin11(_74245_3_pin11), .pin12(_74245_3_pin12), .pin13(_74245_3_pin13), .pin14(_74245_3_pin14),
    .pin15(_74245_3_pin15), .pin16(_74245_3_pin16), .pin17(_74245_3_pin17), .pin18(_74245_3_pin18),
    .pin19(nPAIR_BCOUT), .pin20(VCC));
  _74245 _74245_4 (
    .pin1(VCC), .pin2(_74573_2_pin19), .pin3(_74573_2_pin18), .pin4(_74573_2_pin17), .pin5(_74573_2_pin16),
    .pin6(_74573_2_pin15), .pin7(_74573_2_pin14), .pin8(_74573_2_pin13), .pin9(_74573_2_pin12), .pin10(GND),
    .pin11(_74245_4_pin11), .pin12(_74245_4_pin12), .pin13(_74245_4_pin13), .pin14(_74245_4_pin14),
    .pin15(_74245_4_pin15), .pin16(_74245_4_pin16), .pin17(_74245_4_pin17), .pin18(_74245_4_pin18),
    .pin19(nPAIR_BCOUT), .pin20(VCC));
  BusSplitter #(.Bits(16)) bussplitter_2 (
    .D(ADDR_BUS), .OE(GND), .D0(_74245_3_pin18), .D1(_74245_3_pin17), .D2(_74245_3_pin16),
    .D3(_74245_3_pin15), .D4(_74245_3_pin14), .D5(_74245_3_pin13), .D6(_74245_3_pin12), .D7(_74245_3_pin11),
    .D8(_74245_4_pin18), .D9(_74245_4_pin17), .D10(_74245_4_pin16), .D11(_74245_4_pin15),
    .D12(_74245_4_pin14), .D13(_74245_4_pin13), .D14(_74245_4_pin12), .D15(_74245_4_pin11));

  // Notes on the sheet:
  //   VCC: default 1
  //   nREG_BOUT: default 1
  //   nREG_COUT: default 1
  //   nPAIR_BCOUT: default 1
endmodule
