// Digital circuit register_d_e.dig as structural Verilog
module register_d_e (
  input  REG_DIN,
  input  CLK,
  input  REG_EIN,
  input  VCC,
  input  GND,
  input  [7:0] BUS,
  input  nREG_DOUT,
  input  nREG_EOUT,
  input  nPAIR_DEOUT,
  output [15:0] ADDR_BUS,
  output [7:0] REG_DINT,
  output [7:0] REG_EINT
);

  wire _74245_3_pin11, _74245_3_pin12, _74245_3_pin13, _74245_3_pin14, _74245_3_pin15, _74245_3_pin16,
       _74245_3_pin17, _74245_3_pin18, _74245_4_pin11, _74245_4_pin12, _74245_4_pin13, _74245_4_pin14,
       _74245_4_pin15, _74245_4_pin16, _74245_4_pin17, _74245_4_pin18, _74573_1_pin11, _74573_2_pin11,
       and_1_out, bussplitter_1_d0, bussplitter_1_d1, bussplitter_1_d2, bussplitter_1_d3, bussplitter_1_d4,
       bussplitter_1_d5, bussplitter_1_d6, bussplitter_1_d7;

  and and_1 (and_1_out, nREG_DOUT, nREG_EOUT);
  BusSplitter #(.Bits(8)) bussplitter_1 (
    .D(BUS), .OE(and_1_out), .D0(bussplitter_1_d0), .D1(bussplitter_1_d1), .D2(bussplitter_1_d2),
    .D3(bussplitter_1_d3), .D4(bussplitter_1_d4), .D5(bussplitter_1_d5), .D6(bussplitter_1_d6),
    .D7(bussplitter_1_d7));
  PowerSupply powersupply_1 (.VDD(VCC), .GND(GND));
  _74573 _74573_1 (
    .pin1(GND), .pin2(bussplitter_1_d0), .pin3(bussplitter_1_d1), .pin4(bussplitter_1_d2),
    .pin5(bussplitter_1_d3), .pin6(bussplitter_1_d4), .pin7(bussplitter_1_d5), .pin8(bussplitter_1_d6),
    .pin9(bussplitter_1_d7), .pin10(GND), .pin11(_74573_1_pin11), .pin12(REG_DINT[7]), .pin13(REG_DINT[6]),
    .pin14(REG_DINT[5]), .pin15(REG_DINT[4]), .pin16(REG_DINT[3]), .pin17(REG_DINT[2]), .pin18(REG_DINT[1]),
    .pin19(REG_DINT[0]), .pin20(VCC));
  and and_2 (_74573_1_pin11, REG_DIN, CLK);
  _74573 _74573_2 (
    .pin1(GND), .pin2(bussplitter_1_d0), .pin3(bussplitter_1_d1), .pin4(bussplitter_1_d2),
    .pin5(bussplitter_1_d3), .pin6(bussplitter_1_d4), .pin7(bussplitter_1_d5), .pin8(bussplitter_1_d6),
    .pin9(bussplitter_1_d7), .pin10(GND), .pin11(_74573_2_pin11), .pin12(REG_EINT[7]), .pin13(REG_EINT[6]),
    .pin14(REG_EINT[5]), .pin15(REG_EINT[4]), .pin16(REG_EINT[3]), .pin17(REG_EINT[2]), .pin18(REG_EINT[1]),
    .pin19(REG_EINT[0]), .pin20(VCC));
  and and_3 (_74573_2_pin11, REG_EIN, CLK);
  LED led_1 (.in(REG_DINT[0]));
  LED led_2 (.in(REG_DINT[1]));
  LED led_3 (.in(REG_DINT[2]));
  LED led_4 (.in(REG_DINT[3]));
  LED led_5 (.in(REG_DINT[4]));
  LED led_6 (.in(REG_DINT[5]));
  LED led_7 (.in(REG_DINT[6]));
  LED led_8 (.in(REG_DINT[7]));
  LED led_9 (.in(REG_EINT[0]));
  LED led_10 (.in(REG_EINT[1]));
  LED led_11 (.in(REG_EINT[2]));
  LED led_12 (.in(REG_EINT[3]));
  LED led_13 (.in(REG_EINT[4]));
  LED led_14 (.in(REG_EINT[5]));
  LED led_15 (.in(REG_EINT[6]));
  LED led_16 (.in(REG_EINT[7]));
  _74245 _74245_1 (
    .pin1(VCC), .pin2(REG_DINT[0]), .pin3(REG_DINT[1]), .pin4(REG_DINT[2]), .pin5(REG_DINT[3]),
    .pin6(REG_DINT[4]), .pin7(REG_DINT[5]), .pin8(REG_DINT[6]), .pin9(REG_DINT[7]), .pin10(GND),
    .pin11(bussplitter_1_d7), .pin12(bussplitter_1_d6), .pin13(bussplitter_1_d5), .pin14(bussplitter_1_d4),
    .pin15(bussplitter_1_d3), .pin16(bussplitter_1_d2), .pin17(bussplitter_1_d1), .pin18(bussplitter_1_d0),
    .pin19(nREG_DOUT), .pin20(VCC));
  _74245 _74245_2 (
    .pin1(VCC), .pin2(REG_EINT[0]), .pin3(REG_EINT[1]), .pin4(REG_EINT[2]), .pin5(REG_EINT[3]),
    .pin6(REG_EINT[4]), .pin7(REG_EINT[5]), .pin8(REG_EINT[6]), .pin9(REG_EINT[7]), .pin10(GND),
    .pin11(bussplitter_1_d7), .pin12(bussplitter_1_d6), .pin13(bussplitter_1_d5), .pin14(bussplitter_1_d4),
    .pin15(bussplitter_1_d3), .pin16(bussplitter_1_d2), .pin17(bussplitter_1_d1), .pin18(bussplitter_1_d0),
    .pin19(nREG_EOUT), .pin20(VCC));
  _74245 _74245_3 (
    .pin1(VCC), .pin2(REG_DINT[0]), .pin3(REG_DINT[1]), .pin4(REG_DINT[2]), .pin5(REG_DINT[3]),
    .pin6(REG_DINT[4]), .pin7(REG_DINT[5]), .pin8(REG_DINT[6]), .pin9(REG_DINT[7]), .pin10(GND),
    .pin11(_74245_3_pin11), .pin12(_74245_3_pin12), .pin13(_74245_3_pin13), .pin14(_74245_3_pin14),
    .pin15(_74245_3_pin15), .pin16(_74245_3_pin16), .pin17(_74245_3_pin17), .pin18(_74245_3_pin18),
    .pin19(nPAIR_DEOUT), .pin20(VCC));
  _74245 _74245_4 (
    .pin1(VCC), .pin2(REG_EINT[0]), .pin3(REG_EINT[1]), .pin4(REG_EINT[2]), .pin5(REG_EINT[3]),
    .pin6(REG_EINT[4]), .pin7(REG_EINT[5]), .pin8(REG_EINT[6]), .pin9(REG_EINT[7]), .pin10(GND),
    .pin11(_74245_4_pin11), .pin12(_74245_4_pin12), .pin13(_74245_4_pin13), .pin14(_74245_4_pin14),
    .pin15(_74245_4_pin15), .pin16(_74245_4_pin16), .pin17(_74245_4_pin17), .pin18(_74245_4_pin18),
    .pin19(nPAIR_DEOUT), .pin20(VCC));
  BusSplitter #(.Bits(16)) bussplitter_2 (
    .D(ADDR_BUS), .OE(GND), .D0(_74245_3_pin18), .D1(_74245_3_pin17), .D2(_74245_3_pin16),
    .D3(_74245_3_pin15), .D4(_74245_3_pin14), .D5(_74245_3_pin13), .D6(_74245_3_pin12), .D7(_74245_3_pin11),
    .D8(_74245_4_pin18), .D9(_74245_4_pin17), .D10(_74245_4_pin16), .D11(_74245_4_pin15),
    .D12(_74245_4_pin14), .D13(_74245_4_pin13), .D14(_74245_4_pin12), .D15(_74245_4_pin11));
  // Pins of 1 and 8 bits meet at REG_DINT
  // Pins of 1 and 8 bits meet at REG_EINT

  // Notes on the sheet:
  //   VCC: default 1
  //   nREG_DOUT: default 1
  //   nREG_EOUT: default 1
  //   nPAIR_DEOUT: default 1
endmodule
