// Digital circuit register_h_l.dig as structural Verilog
module register_h_l (
  input  [7:0] BUS,
  input  nDEC_H,
  input  REG_LIN,
  input  REG_HIN,
  input  RST,
  input  VCC,
  input  GND,
  input  nREG_LOUT,
  input  nREG_HOUT,
  input  nPAIR_HLOUT,
  input  nINC_H,
  input  clk,
  output [15:0] ADDR_BUS
);

  wire _74193_1_pin2, _74193_1_pin3, _74193_1_pin6, _74193_1_pin7, _74193_1_pin12, _74193_1_pin13,
       _74193_2_pin2, _74193_2_pin3, _74193_2_pin6, _74193_2_pin7, _74193_2_pin12, _74193_2_pin13,
       _74193_3_pin2, _74193_3_pin3, _74193_3_pin6, _74193_3_pin7, _74193_3_pin12, _74193_3_pin13,
       _74193_4_pin2, _74193_4_pin3, _74193_4_pin6, _74193_4_pin7, _74245_3_pin11, _74245_3_pin12,
       _74245_3_pin13, _74245_3_pin14, _74245_3_pin15, _74245_3_pin16, _74245_3_pin17, _74245_3_pin18,
       _74245_4_pin11, _74245_4_pin12, _74245_4_pin13, _74245_4_pin14, _74245_4_pin15, _74245_4_pin16,
       _74245_4_pin17, _74245_4_pin18, and_1_out, bussplitter_1_d0, bussplitter_1_d1, bussplitter_1_d2,
       bussplitter_1_d3, bussplitter_1_d4, bussplitter_1_d5, bussplitter_1_d6, bussplitter_1_d7, nand_1_out,
       nand_2_out;

  and and_1 (and_1_out, nREG_LOUT, nREG_HOUT);
  BusSplitter #(.Bits(8)) bussplitter_1 (
    .D(BUS), .OE(and_1_out), .D0(bussplitter_1_d0), .D1(bussplitter_1_d1), .D2(bussplitter_1_d2),
    .D3(bussplitter_1_d3), .D4(bussplitter_1_d4), .D5(bussplitter_1_d5), .D6(bussplitter_1_d6),
    .D7(bussplitter_1_d7));
  nand nand_1 (nand_1_out, REG_LIN, clk);
  nand nand_2 (nand_2_out, clk, REG_HIN);
  PowerSupply powersupply_1 (.VDD(VCC), .GND(GND));
  _74193 _74193_1 (
    .pin1(bussplitter_1_d1), .pin2(_74193_1_pin2), .pin3(_74193_1_pin3), .pin4(nDEC_H), .pin5(nINC_H),
    .pin6(_74193_1_pin6), .pin7(_74193_1_pin7), .pin8(GND), .pin9(bussplitter_1_d3),
    .pin10(bussplitter_1_d2), .pin11(nand_1_out), .pin12(_74193_1_pin12), .pin13(_74193_1_pin13),
    .pin14(RST), .pin15(bussplitter_1_d0), .pin16(VCC));
  _74193 _74193_2 (
    .pin1(bussplitter_1_d5), .pin2(_74193_2_pin2), .pin3(_74193_2_pin3), .pin4(_74193_1_pin13),
    .pin5(_74193_1_pin12), .pin6(_74193_2_pin6), .pin7(_74193_2_pin7), .pin8(GND), .pin9(bussplitter_1_d7),
    .pin10(bussplitter_1_d6), .pin11(nand_1_out), .pin12(_74193_2_pin12), .pin13(_74193_2_pin13),
    .pin14(RST), .pin15(bussplitter_1_d4), .pin16(VCC));
  _74193 _74193_3 (
    .pin1(bussplitter_1_d1), .pin2(_74193_3_pin2), .pin3(_74193_3_pin3), .pin4(_74193_2_pin13),
    .pin5(_74193_2_pin12), .pin6(_74193_3_pin6), .pin7(_74193_3_pin7), .pin8(GND), .pin9(bussplitter_1_d3),
    .pin10(bussplitter_1_d2), .pin11(nand_2_out), .pin12(_74193_3_pin12), .pin13(_74193_3_pin13),
    .pin14(RST), .pin15(bussplitter_1_d0), .pin16(VCC));
  _74193 _74193_4 (
    .pin1(bussplitter_1_d5), .pin2(_74193_4_pin2), .pin3(_74193_4_pin3), .pin4(_74193_3_pin13),
    .pin5(_74193_3_pin12), .pin6(_74193_4_pin6), .pin7(_74193_4_pin7), .pin8(GND), .pin9(bussplitter_1_d7),
    .pin10(bussplitter_1_d6), .pin11(nand_2_out), .pin14(RST), .pin15(bussplitter_1_d4), .pin16(VCC));  // open: pin12, pin13
  LED led_1 (.in(_74193_4_pin7));
  LED led_2 (.in(_74193_4_pin6));
  LED led_3 (.in(_74193_4_pin2));
  LED led_4 (.in(_74193_4_pin3));
  LED led_5 (.in(_74193_3_pin7));
  LED led_6 (.in(_74193_3_pin6));
  LED led_7 (.in(_74193_3_pin2));
  LED led_8 (.in(_74193_3_pin3));
  LED led_9 (.in(_74193_2_pin7));
  LED led_10 (.in(_74193_2_pin6));
  LED led_11 (.in(_74193_2_pin2));
  LED led_12 (.in(_74193_2_pin3));
  LED led_13 (.in(_74193_1_pin7));
  LED led_14 (.in(_74193_1_pin6));
  LED led_15 (.in(_74193_1_pin2));
  LED led_16 (.in(_74193_1_pin3));
  _74245 _74245_1 (
    .pin1(VCC), .pin2(_74193_1_pin3), .pin3(_74193_1_pin2), .pin4(_74193_1_pin6), .pin5(_74193_1_pin7),
    .pin6(_74193_2_pin3), .pin7(_74193_2_pin2), .pin8(_74193_2_pin6), .pin9(_74193_2_pin7), .pin10(GND),
    .pin11(bussplitter_1_d7), .pin12(bussplitter_1_d6), .pin13(bussplitter_1_d5), .pin14(bussplitter_1_d4),
    .pin15(bussplitter_1_d3), .pin16(bussplitter_1_d2), .pin17(bussplitter_1_d1), .pin18(bussplitter_1_d0),
    .pin19(nREG_LOUT), .pin20(VCC));
  _74245 _74245_2 (
    .pin1(VCC), .pin2(_74193_3_pin3), .pin3(_74193_3_pin2), .pin4(_74193_3_pin6), .pin5(_74193_3_pin7),
    .pin6(_74193_4_pin3), .pin7(_74193_4_pin2), .pin8(_74193_4_pin6), .pin9(_74193_4_pin7), .pin10(GND),
    .pin11(bussplitter_1_d7), .pin12(bussplitter_1_d6), .pin13(bussplitter_1_d5), .pin14(bussplitter_1_d4),
    .pin15(bussplitter_1_d3), .pin16(bussplitter_1_d2), .pin17(bussplitter_1_d1), .pin18(bussplitter_1_d0),
    .pin19(nREG_HOUT), .pin20(VCC));
  _74245 _74245_3 (
    .pin1(VCC), .pin2(_74193_1_pin3), .pin3(_74193_1_pin2), .pin4(_74193_1_pin6), .pin5(_74193_1_pin7),
    .pin6(_74193_2_pin3), .pin7(_74193_2_pin2), .pin8(_74193_2_pin6), .pin9(_74193_2_pin7), .pin10(GND),
    .pin11(_74245_3_pin11), .pin12(_74245_3_pin12), .pin13(_74245_3_pin13), .pin14(_74245_3_pin14),
    .pin15(_74245_3_pin15), .pin16(_74245_3_pin16), .pin17(_74245_3_pin17), .pin18(_74245_3_pin18),
    .pin19(nPAIR_HLOUT), .pin20(VCC));
  _74245 _74245_4 (
    .pin1(VCC), .pin2(_74193_3_pin3), .pin3(_74193_3_pin2), .pin4(_74193_3_pin6), .pin5(_74193_3_pin7),
    .pin6(_74193_4_pin3), .pin7(_74193_4_pin2), .pin8(_74193_4_pin6), .pin9(_74193_4_pin7), .pin10(GND),
    .pin11(_74245_4_pin11), .pin12(_74245_4_pin12), .pin13(_74245_4_pin13), .pin14(_74245_4_pin14),
    .pin15(_74245_4_pin15), .pin16(_74245_4_pin16), .pin17(_74245_4_pin17), .pin18(_74245_4_pin18),
    .pin19(nPAIR_HLOUT), .pin20(VCC));
  BusSplitter #(.Bits(16)) bussplitter_2 (
    .D(ADDR_BUS), .OE(GND), .D0(_74245_3_pin18), .D1(_74245_3_pin17), .D2(_74245_3_pin16),
    .D3(_74245_3_pin15), .D4(_74245_3_pin14), .D5(_74245_3_pin13), .D6(_74245_3_pin12), .D7(_74245_3_pin11),
    .D8(_74245_4_pin18), .D9(_74245_4_pin17), .D10(_74245_4_pin16), .D11(_74245_4_pin15),
    .D12(_74245_4_pin14), .D13(_74245_4_pin13), .D14(_74245_4_pin12), .D15(_74245_4_pin11));

  // Notes on the sheet:
  //   nDEC_H: default 1
  //   VCC: default 1
  //   nREG_LOUT: default 1
  //   nREG_HOUT: default 1
  //   nPAIR_HLOUT: default 1
  //   nINC_H: default 1
endmodule
