// Digital circuit register_instruction.dig as structural Verilog
module register_instruction (
  input  [7:0] BUS,
  input  CLK,
  input  IR_IN,
  input  VCC,
  input  GND,
  output [7:0] IR_BUS
);

  wire _74573_1_pin11, _74573_1_pin12, _74573_1_pin13, _74573_1_pin14, _74573_1_pin15, _74573_1_pin16,
       _74573_1_pin17, _74573_1_pin18, _74573_1_pin19, bussplitter_1_d0, bussplitter_1_d1, bussplitter_1_d2,
       bussplitter_1_d3, bussplitter_1_d4, bussplitter_1_d5, bussplitter_1_d6, bussplitter_1_d7;

  BusSplitter #(.Bits(8)) bussplitter_1 (
    .D(BUS), .OE(VCC), .D0(bussplitter_1_d0), .D1(bussplitter_1_d1), .D2(bussplitter_1_d2),
    .D3(bussplitter_1_d3), .D4(bussplitter_1_d4), .D5(bussplitter_1_d5), .D6(bussplitter_1_d6),
    .D7(bussplitter_1_d7));
  PowerSupply powersupply_1 (.VDD(VCC), .GND(GND));
  _74573 _74573_1 (
    .pin1(GND), .pin2(bussplitter_1_d0), .pin3(bussplitter_1_d1), .pin4(bussplitter_1_d2),
    .pin5(bussplitter_1_d3), .pin6(bussplitter_1_d4), .pin7(bussplitter_1_d5), .pin8(bussplitter_1_d6),
    .pin9(bussplitter_1_d7), .pin10(GND), .pin11(_74573_1_pin11), .pin12(_74573_1_pin12),
    .pin13(_74573_1_pin13), .pin14(_74573_1_pin14), .pin15(_74573_1_pin15), .pin16(_74573_1_pin16),
    .pin17(_74573_1_pin17), .pin18(_74573_1_pin18), .pin19(_74573_1_pin19), .pin20(VCC));
  and and_1 (_74573_1_pin11, IR_IN, CLK);
  LED led_1 (.in(_74573_1_pin19));
  LED led_2 (.in(_74573_1_pin18));
  LED led_3 (.in(_74573_1_pin17));
  LED led_4 (.in(_74573_1_pin16));
  LED led_5 (.in(_74573_1_pin15));
  LED led_6 (.in(_74573_1_pin14));
  LED led_7 (.in(_74573_1_pin13));
  LED led_8 (.in(_74573_1_pin12));
  BusSplitter #(.Bits(8)) bussplitter_2 (
    .D(IR_BUS), .OE(GND), .D0(_74573_1_pin19), .D1(_74573_1_pin18), .D2(_74573_1_pin17), .D3(_74573_1_pin16),
    .D4(_74573_1_pin15), .D5(_74573_1_pin14), .D6(_74573_1_pin13), .D7(_74573_1_pin12));

  // Notes on the sheet:
  //   VCC: default 1
endmodule
