// Digital circuit register_output.dig as structural Verilog
module register_output (
  input  CLK,
  input  REG_OUTIN,
  input  CLK_DISP,
  input  [7:0] BUS,
  input  VCC,
  input  GND,
  output [11:0] LED_SEGOUT
);

  wire _74107_1_pin2, _74139_1_pin9, _74139_1_pin10, _74139_1_pin11, _74139_1_pin12, _74139_1_pin13,
       _74139_1_pin14, _74139_1_pin15, _74573_1_pin11, bussplitter_1_d0, bussplitter_1_d1, bussplitter_1_d2,
       bussplitter_1_d3, bussplitter_1_d4, bussplitter_1_d5, bussplitter_1_d6, bussplitter_1_d7, nor_1_out;
  wire [7:0] eeprom_d;
  wire [9:0] _74573_1_pin19;

  BusSplitter #(.Bits(8)) bussplitter_1 (
    .D(BUS), .OE(VCC), .D0(bussplitter_1_d0), .D1(bussplitter_1_d1), .D2(bussplitter_1_d2),
    .D3(bussplitter_1_d3), .D4(bussplitter_1_d4), .D5(bussplitter_1_d5), .D6(bussplitter_1_d6),
    .D7(bussplitter_1_d7));
  _74573 _74573_1 (
    .pin1(GND), .pin2(bussplitter_1_d0), .pin3(bussplitter_1_d1), .pin4(bussplitter_1_d2),
    .pin5(bussplitter_1_d3), .pin6(bussplitter_1_d4), .pin7(bussplitter_1_d5), .pin8(bussplitter_1_d6),
    .pin9(bussplitter_1_d7), .pin10(GND), .pin11(_74573_1_pin11), .pin12(_74573_1_pin19[7]),
    .pin13(_74573_1_pin19[6]), .pin14(_74573_1_pin19[5]), .pin15(_74573_1_pin19[4]),
    .pin16(_74573_1_pin19[3]), .pin17(_74573_1_pin19[2]), .pin18(_74573_1_pin19[1]),
    .pin19(_74573_1_pin19[0]), .pin20(VCC));
  and and_1 (_74573_1_pin11, REG_OUTIN, CLK);
  _74107 _74107_1 (
    .pin1(VCC), .pin2(_74107_1_pin2), .pin3(_74573_1_pin19[9]), .pin4(VCC), .pin5(_74573_1_pin19[8]),
    .pin7(GND), .pin8(VCC), .pin9(_74107_1_pin2), .pin10(VCC), .pin11(VCC), .pin12(CLK_DISP), .pin13(VCC),
    .pin14(VCC));  // open: pin6
  PowerSupply powersupply_1 (.VDD(VCC), .GND(GND));
  _74139 _74139_1 (
    .pin1(GND), .pin2(_74573_1_pin19[9]), .pin3(_74573_1_pin19[8]), .pin4(LED_SEGOUT[11]),
    .pin5(LED_SEGOUT[9]), .pin6(LED_SEGOUT[10]), .pin7(LED_SEGOUT[8]), .pin8(GND), .pin9(_74139_1_pin9),
    .pin10(_74139_1_pin10), .pin11(_74139_1_pin11), .pin12(_74139_1_pin12), .pin13(_74139_1_pin13),
    .pin14(_74139_1_pin14), .pin15(_74139_1_pin15), .pin16(VCC));
  EEPROM #(.AddrBits(13), .Bits(8)) eeprom (
    .A({{3{GND}}, _74573_1_pin19}), .CS(~GND), .WE(~VCC), .OE(~GND), .D(eeprom_d));
  nor nor_1 (nor_1_out, GND, ~VCC, GND);  // NOr
  // NotConnected on _74139_1_pin15
  // NotConnected on _74139_1_pin14
  // NotConnected on _74139_1_pin13
  BusSplitter #(.Bits(8)) bussplitter_2 (
    .D(eeprom_d), .OE(nor_1_out), .D0(LED_SEGOUT[0]), .D1(LED_SEGOUT[1]), .D2(LED_SEGOUT[2]),
    .D3(LED_SEGOUT[3]), .D4(LED_SEGOUT[4]), .D5(LED_SEGOUT[5]), .D6(LED_SEGOUT[6]), .D7(LED_SEGOUT[7]));
  Seven_Seg #(.commonCathode("true"), .persistTime(10)) seven_seg_1 (
    .a(LED_SEGOUT[1]), .b(LED_SEGOUT[2]), .c(LED_SEGOUT[3]), .d(LED_SEGOUT[4]), .e(LED_SEGOUT[5]),
    .f(LED_SEGOUT[6]), .g(LED_SEGOUT[7]), .dp(LED_SEGOUT[0]), .common(LED_SEGOUT[8]));
  Seven_Seg #(.commonCathode("true"), .persistTime(10)) seven_seg_2 (
    .a(LED_SEGOUT[1]), .b(LED_SEGOUT[2]), .c(LED_SEGOUT[3]), .d(LED_SEGOUT[4]), .e(LED_SEGOUT[5]),
    .f(LED_SEGOUT[6]), .g(LED_SEGOUT[7]), .dp(LED_SEGOUT[0]), .common(LED_SEGOUT[9]));
  Seven_Seg #(.commonCathode("true"), .persistTime(10)) seven_seg_3 (
    .a(LED_SEGOUT[1]), .b(LED_SEGOUT[2]), .c(LED_SEGOUT[3]), .d(LED_SEGOUT[4]), .e(LED_SEGOUT[5]),
    .f(LED_SEGOUT[6]), .g(LED_SEGOUT[7]), .dp(LED_SEGOUT[0]), .common(LED_SEGOUT[10]));
  Seven_Seg #(.commonCathode("true"), .persistTime(10)) seven_seg_4 (
    .a(LED_SEGOUT[1]), .b(LED_SEGOUT[2]), .c(LED_SEGOUT[3]), .d(LED_SEGOUT[4]), .e(LED_SEGOUT[5]),
    .f(LED_SEGOUT[6]), .g(LED_SEGOUT[7]), .dp(LED_SEGOUT[0]), .common(LED_SEGOUT[11]));

  // Notes on the sheet:
  //   CLK_DISP: Hz: 1000
  //   VCC: default 1
  //   contents of eeprom (hex, n*v repeats v):
  //   7e,c,b6,9e,cc,da,fa,e,fe,de,7e,c,b6,9e,cc,da,fa,e,fe,de,7e,c,b6
  //   ,9e,cc,da,fa,e,fe,de,7e,c,b6,9e,cc,da,fa,e,fe,de,7e,c,b6,9e,cc
  //   ,da,fa,e,fe,de,7e,c,b6,9e,cc,da,fa,e,fe,de,7e,c,b6,9e,cc,da,fa
  //   ,e,fe,de,7e,c,b6,9e,cc,da,fa,e,fe,de,7e,c,b6,9e,cc,da,fa,e,fe
  //   ,de,7e,c,b6,9e,cc,da,fa,e,fe,de,7e,c,b6,9e,cc,da,fa,e,fe,de,7e
  //   ,c,b6,9e,cc,da,fa,e,fe,de,7e,c,b6,9e,cc,da,fa,e,fe,de,7e,c,b6
  //   ,9e,cc,da,fa,e,fe,de,7e,c,b6,9e,cc,da,fa,e,fe,de,7e,c,b6,9e,cc
  //   ,da,fa,e,fe,de,7e,c,b6,9e,cc,da,fa,e,fe,de,7e,c,b6,9e,cc,da,fa
  //   ,e,fe,de,7e,c,b6,9e,cc,da,fa,e,fe,de,7e,c,b6,9e,cc,da,fa,e,fe
  //   ,de,7e,c,b6,9e,cc,da,fa,e,fe,de,7e,c,b6,9e,cc,da,fa,e,fe,de,7e
  //   ,c,b6,9e,cc,da,fa,e,fe,de,7e,c,b6,9e,cc,da,fa,e,fe,de,7e,c,b6
  //   ,9e,cc,da,fa,e,fe,de,7e,c,b6,9e,cc,da,10*7e,10*c,10*b6,10*9e,10*cc
  //   ,10*da,10*fa,10*e,10*fe,10*de,10*7e,10*c,10*b6,10*9e,10*cc,10*da
  //   ,10*fa,10*e,10*fe,10*de,10*7e,10*c,10*b6,10*9e,10*cc,6*da,100*7e
  //   ,100*c,56*b6
endmodule
