// Digital circuit register_temporary.dig as structural Verilog
module register_temporary (
  input  VCC,
  input  GND,
  input  REG_TIN,
  input  CLK,
  input  nREG_TOUT,
  input  [7:0] BUS,
  output [7:0] REG_TINT
);

  wire _74573_1_pin11, _74573_1_pin12, _74573_1_pin13, _74573_1_pin14, _74573_1_pin15, _74573_1_pin16,
       _74573_1_pin17, _74573_1_pin18, _74573_1_pin19, bussplitter_1_d0, bussplitter_1_d1, bussplitter_1_d2,
       bussplitter_1_d3, bussplitter_1_d4, bussplitter_1_d5, bussplitter_1_d6, bussplitter_1_d7;

  PowerSupply powersupply_1 (.VDD(VCC), .GND(GND));
  BusSplitter #(.Bits(8)) bussplitter_1 (
    .D(BUS), .OE(nREG_TOUT), .D0(bussplitter_1_d0), .D1(bussplitter_1_d1), .D2(bussplitter_1_d2),
    .D3(bussplitter_1_d3), .D4(bussplitter_1_d4), .D5(bussplitter_1_d5), .D6(bussplitter_1_d6),
    .D7(bussplitter_1_d7));
  LED led_1 (.in(bussplitter_1_d6));
  LED led_2 (.in(bussplitter_1_d7));
  _74573 _74573_1 (
    .pin1(GND), .pin2(bussplitter_1_d0), .pin3(bussplitter_1_d1), .pin4(bussplitter_1_d2),
    .pin5(bussplitter_1_d3), .pin6(bussplitter_1_d4), .pin7(bussplitter_1_d5), .pin8(bussplitter_1_d6),
    .pin9(bussplitter_1_d7), .pin10(GND), .pin11(_74573_1_pin11), .pin12(_74573_1_pin12),
    .pin13(_74573_1_pin13), .pin14(_74573_1_pin14), .pin15(_74573_1_pin15), .pin16(_74573_1_pin16),
    .pin17(_74573_1_pin17), .pin18(_74573_1_pin18), .pin19(_74573_1_pin19), .pin20(VCC));
  LED led_3 (.in(bussplitter_1_d4));
  LED led_4 (.in(bussplitter_1_d5));
  and and_1 (_74573_1_pin11, REG_TIN, CLK);
  LED led_5 (.in(bussplitter_1_d2));
  LED led_6 (.in(bussplitter_1_d3));
  LED led_7 (.in(bussplitter_1_d0));
  LED led_8 (.in(bussplitter_1_d1));
  LED led_9 (.in(_74573_1_pin19));
  LED led_10 (.in(_74573_1_pin18));
  LED led_11 (.in(_74573_1_pin17));
  LED led_12 (.in(_74573_1_pin16));
  LED led_13 (.in(_74573_1_pin15));
  LED led_14 (.in(_74573_1_pin14));
  LED led_15 (.in(_74573_1_pin13));
  LED led_16 (.in(_74573_1_pin12));
  BusSplitter #(.Bits(8)) bussplitter_2 (
    .D(REG_TINT), .OE(GND), .D0(_74573_1_pin19), .D1(_74573_1_pin18), .D2(_74573_1_pin17),
    .D3(_74573_1_pin16), .D4(_74573_1_pin15), .D5(_74573_1_pin14), .D6(_74573_1_pin13), .D7(_74573_1_pin12));
  _74245 _74245_1 (
    .pin1(VCC), .pin2(_74573_1_pin19), .pin3(_74573_1_pin18), .pin4(_74573_1_pin17), .pin5(_74573_1_pin16),
    .pin6(_74573_1_pin15), .pin7(_74573_1_pin14), .pin8(_74573_1_pin13), .pin9(_74573_1_pin12), .pin10(GND),
    .pin11(bussplitter_1_d7), .pin12(bussplitter_1_d6), .pin13(bussplitter_1_d5), .pin14(bussplitter_1_d4),
    .pin15(bussplitter_1_d3), .pin16(bussplitter_1_d2), .pin17(bussplitter_1_d1), .pin18(bussplitter_1_d0),
    .pin19(nREG_TOUT), .pin20(VCC));

  // Notes on the sheet:
  //   VCC: default 1
  //   nREG_TOUT: default 1
endmodule
