// Digital circuit rom.dig as structural Verilog
module rom (
  input  nROM_CS,
  input  VCC,
  input  GND,
  input  [7:0] ROM_DATAIN,
  input  PROG_ROM,
  input  [15:0] ADDR_BUS,
  output [7:0] BUS,
  output [7:0] ROM_INT
);

  wire _74245_1_pin19, nor_1_out;
  wire [7:0] eeprom_d;

  EEPROM #(.AddrBits(13), .Bits(8)) eeprom (
    .A(ADDR_BUS[12:0]), .CS(~nROM_CS), .WE(~_74245_1_pin19), .OE(~GND), .D(eeprom_d));
  nor nor_1 (nor_1_out, nROM_CS, ~_74245_1_pin19, GND);  // NOr
  BusSplitter #(.Bits(8)) bussplitter_1 (
    .D(eeprom_d), .OE(nor_1_out), .D0(ROM_INT[0]), .D1(ROM_INT[1]), .D2(ROM_INT[2]), .D3(ROM_INT[3]),
    .D4(ROM_INT[4]), .D5(ROM_INT[5]), .D6(ROM_INT[6]), .D7(ROM_INT[7]));
  LED led_1 (.in(ROM_INT[0]));
  LED led_2 (.in(ROM_INT[1]));
  LED led_3 (.in(ROM_INT[2]));
  LED led_4 (.in(ROM_INT[3]));
  LED led_5 (.in(ROM_INT[4]));
  LED led_6 (.in(ROM_INT[5]));
  LED led_7 (.in(ROM_INT[6]));
  LED led_8 (.in(ROM_INT[7]));
  _74245 _74245_1 (
    .pin1(VCC), .pin2(ROM_DATAIN[0]), .pin3(ROM_DATAIN[1]), .pin4(ROM_DATAIN[2]), .pin5(ROM_DATAIN[3]),
    .pin6(ROM_DATAIN[4]), .pin7(ROM_DATAIN[5]), .pin8(ROM_DATAIN[6]), .pin9(ROM_DATAIN[7]), .pin10(GND),
    .pin11(ROM_INT[7]), .pin12(ROM_INT[6]), .pin13(ROM_INT[5]), .pin14(ROM_INT[4]), .pin15(ROM_INT[3]),
    .pin16(ROM_INT[2]), .pin17(ROM_INT[1]), .pin18(ROM_INT[0]), .pin19(_74245_1_pin19), .pin20(VCC));
  not not_1 (_74245_1_pin19, PROG_ROM);
  PowerSupply powersupply_1 (.VDD(VCC), .GND(GND));
  _74245 _74245_2 (
    .pin1(VCC), .pin2(ROM_INT[0]), .pin3(ROM_INT[1]), .pin4(ROM_INT[2]), .pin5(ROM_INT[3]),
    .pin6(ROM_INT[4]), .pin7(ROM_INT[5]), .pin8(ROM_INT[6]), .pin9(ROM_INT[7]), .pin10(GND), .pin11(BUS[7]),
    .pin12(BUS[6]), .pin13(BUS[5]), .pin14(BUS[4]), .pin15(BUS[3]), .pin16(BUS[2]), .pin17(BUS[1]),
    .pin18(BUS[0]), .pin19(nROM_CS), .pin20(VCC));

  // Notes on the sheet:
  //   nROM_CS: pin 20, default 1
  //   VCC: default 1
  //   contents of eeprom (hex, n*v repeats v):
  //   ff,56,aa,55,d5,80,0,0,3
endmodule
