// Digital circuit step_counter.dig as structural Verilog
module step_counter (
  input  nCLK,
  input  VCC,
  input  GND,
  input  SC_RST,
  input  RST,
  output STEP_0,
  output STEP_1,
  output STEP_2,
  output STEP_3,
  output CLR
);

  wire _74161_1_pin1, _74161_1_pin3, _74161_1_pin4, _74161_1_pin5, _74161_1_pin6, _74161_1_pin15;

  PowerSupply powersupply_1 (.VDD(VCC), .GND(GND));
  not not_1 (CLR, _74161_1_pin1);
  _74161 _74161_1 (
    .pin1(_74161_1_pin1), .pin2(nCLK), .pin3(_74161_1_pin3), .pin4(_74161_1_pin4), .pin5(_74161_1_pin5),
    .pin6(_74161_1_pin6), .pin7(VCC), .pin8(GND), .pin9(VCC), .pin10(VCC), .pin11(STEP_3), .pin12(STEP_2),
    .pin13(STEP_1), .pin14(STEP_0), .pin15(_74161_1_pin15), .pin16(VCC));
  // NotConnected on _74161_1_pin3
  // NotConnected on _74161_1_pin4
  // NotConnected on _74161_1_pin5
  // NotConnected on _74161_1_pin6
  nor nor_1 (_74161_1_pin1, RST, SC_RST, _74161_1_pin15);
  LED led_1 (.in(STEP_3));
  LED led_2 (.in(STEP_2));
  LED led_3 (.in(STEP_1));
  LED led_4 (.in(STEP_0));

  // Notes on the sheet:
  //   nCLK: default 1
  //   VCC: default 1
endmodule
