// Digital circuit test.dig as structural Verilog
module test (
  input  in_1,
  input  VCC,
  input  GND,
  input  in_4,
  input  in_5
);

  wire STEP_0, STEP_1, STEP_2, STEP_3;

  PowerSupply powersupply_1 (.VDD(VCC), .GND(GND));
  step_counter step_counter_1 (
    .nCLK(in_1), .VCC(VCC), .GND(GND), .SC_RST(in_4), .RST(in_5), .STEP_0(STEP_0), .STEP_1(STEP_1),
    .STEP_2(STEP_2), .STEP_3(STEP_3));  // open: CLR
  LED led_1 (.in(STEP_3));
  LED led_2 (.in(STEP_1));
  LED led_3 (.in(STEP_2));
  LED led_4 (.in(STEP_0));

  // Notes on the sheet:
  //   VCC: default 1
  //   Step
endmodule
